// Logisim project 5cdm16m.circ as structural Verilog: 16 circuits, main circuit cdm16
module register_enable (
  input  busDa,
  input  busDXa,
  input  switcher,
  output out
);

  Multiplexer #(.enable("false")) multiplexer_1 (.in0(busDa), .in1(busDXa), .out(out), .sel(switcher));
endmodule

module multiply (
  input  [15:0] A,
  input  [15:0] B,
  output [15:0] low_bits,
  output [15:0] high_bits,
  output carry_bit
);

  wire zero16_1_zero;

  Multiplier #(.width(16)) multiplier_1 (.a(A), .b(B), .out(low_bits), .cout(high_bits));  // open: cin
  not not_1 (carry_bit, zero16_1_zero);
  zero16 zero16_1 (.in(high_bits), .zero(zero16_1_zero));

  // Other names for the same wires on the sheet: carry = carry_bit; mulhigh[15:0] = high_bits;
  //   mullow[15:0] = low_bits

  // Notes on the sheet:
  //   B: pull=down
  //   A: pull=down
endmodule

module cdm16 (
  input  [15:0] data_in,
  input  EXC,
  input  [5:0] exc_vec,
  input  IRQ,
  input  [5:0] int_vec,
  input  clock,
  input  hold,
  output [15:0] SP,
  output [15:0] PC,
  output [15:0] PS,
  output [15:0] R0,
  output [15:0] R1,
  output [15:0] R2,
  output [15:0] R3,
  output [15:0] R4,
  output [15:0] address,
  output mem,
  output [15:0] R5,
  output data_ins_prime,
  output rd_wr_prime,
  output [15:0] R6,
  output [15:0] FP,
  output word,
  output [15:0] data_out,
  output out_25,
  output [1:0] status,
  output IAck,
  output fetch
);

  wire _0op, _1op, _2op, alu2, alu3, alu3_ind, alu_asrtD, alu_asrtDX, and_2_out, and_4_out, and_7_out,
       and_10_out, and_11_out, and_14_out, and_15_out, and_16_out, and_19_out, and_20_out, and_22_out,
       and_24_out, and_28_out, and_29_out, and_31_out, and_34_out, and_35_out, and_37_out, and_41_out,
       and_42_out, and_43_out, and_44_out, and_45_out, and_48_out, and_50_out, and_52_out, and_54_out,
       and_55_out, and_56_out, and_61_out, and_62_out, and_63_out, arith_carry, br_abs, br_abs_d, br_abs_nop,
       br_rel_n, br_rel_nop, br_rel_p, branch_logic_1_go, clk, clk_inhibit, clk_no_inhibit, comparator_1_eq,
       comparator_3_eq, cout, critical_fault, CUT, d_ff_1_q, d_ff_2_qn, decoder_1_out0, decoder_1_out1,
       decoder_1_out2, decoder_1_out3, decoder_1_out4, decoder_1_out5, decoder_1_out6, decoder_1_out7,
       decoder_3_out0, decoder_3_out1, decoder_3_out2, decoder_3_out3, decoder_3_out4, decoder_3_out5,
       decoder_3_out6, decoder_3_out7, decoder_4_out0, decoder_4_out2, decoder_4_out5, decoder_4_out6,
       decoder_4_out7, demultiplexer_1_out0, di, double_fault, DXa, ei, exc_latch, exc_trig_invalid_inst,
       exc_trig_pc, exc_trig_sp, fp_asrt0, fp_DX_en, fp_s_en, fpDXa, halt, imm6, imm9, imm_asrt1, imm_asrtD,
       imm_extend_negative, imm_shift, inc_address, \int , io_phase, jsr, latch_double_fault, latch_int,
       mem2, mem3, multiplexer_20_out, nor_1_out, not_1_out, not_2_out, not_3_out, not_4_out, not_5_out,
       not_6_out, not_7_out, not_8_out, not_9_out, not_10_out, not_11_out, not_12_out, not_13_out,
       not_14_out, or_1_out, or_2_out, or_3_out, or_4_out, or_5_out, or_10_out, or_11_out, or_13_out,
       or_14_out, or_15_out, or_17_out, or_19_out, or_20_out, or_21_out, or_23_out, or_24_out, pc_asrt0,
       pc_asrtD, pc_inc, pc_inc_inhibit, pc_latch, priority_encoder_2_gs, priority_encoder_4_gs, ps_asrtD,
       ps_latch_flags, ps_latch_word, r0_DX_en, r0_s_en, r0DXa, r1_DX_en, r1_s_en, r1DXa, r2_DX_en, r2_s_en,
       r2DXa, r3_DX_en, r3_s_en, r3DXa, r4_DX_en, r4_s_en, r4DXa, r5_DX_en, r5_s_en, r5DXa, r6_DX_en,
       r6_s_en, r6DXa, r_asrt0, r_asrt1, r_asrtD, r_asrtDX, r_latch, r_latchx, register_enable_1_out,
       register_enable_2_out, register_enable_3_out, register_enable_4_out, register_enable_5_out,
       register_enable_6_out, register_enable_7_out, register_enable_8_out, reset_exc, rti, s_r_ff_1_q,
       s_r_ff_2_q, s_r_ff_3_q, shifts, sign_extend, sp_asrt0, sp_asrtD, sp_dec, sp_inc, sp_latch, startup,
       virtual_instruction, \wait , word_t;
  wire [0:0] or_16_out;
  wire [2:0] alu_func, alu_op_d0, alu_op_d1, alu_op_type, CVZN, exc_internal_vec, multiplexer_6_out,
       multiplexer_31_out, multiplexer_32_out, phase, priority_encoder_2_out, priority_encoder_3_out,
       priority_encoder_4_out, rdX, rs0, rs1;
  wire [2:1] imm6_d;
  wire [3:0] bit_extender_10_out, br_abs_flags_d, multiplexer_19_out, multiplexer_22_out, ps_flags;
  wire [3:3] br_rel_flags_d;
  wire [5:0] exc_vec_t;
  wire [15:0] alu_1_mul_high, bit_extender_1_out, bit_extender_2_out, bit_extender_3_out, bit_extender_4_out,
       bit_extender_5_out, bit_extender_6_out, bit_extender_7_out, bit_extender_8_out, bit_extender_9_out,
       bus0, bus1, bus_control_1_to_bus, busD, busDX, fetched_instruction, imm, multiplexer_1_out,
       multiplexer_2_out, multiplexer_3_out, multiplexer_4_out, multiplexer_5_out, multiplexer_7_out,
       multiplexer_8_out, multiplexer_9_out, multiplexer_10_out, multiplexer_11_out, multiplexer_12_out,
       multiplexer_13_out, multiplexer_16_out, multiplexer_21_out, multiplexer_24_out, multiplexer_25_out,
       or_9_out, or_18_out, pc_register_1_mon, shifter_1_out, shifter_2_out, sp_register_1_mon;
  wire [15:13] register_11_q;
  wire [31:0] multiplexer_29_out, rom_1_data, rom_2_data;

  not not_1 (not_1_out, CUT);
  Register #(.width(6), .trigger("falling")) register_1 (
    .D(exc_vec), .en(EXC), .Q(exc_vec_t), .clk(clk_no_inhibit));  // open: clr
  D_Flip_Flop #(.trigger("low")) d_ff_1 (.clk(clock), .D(hold), .Q(d_ff_1_q));  // open: Qn, preset, en, reset
  S_R_Flip_Flop #(.trigger("falling")) s_r_ff_1 (
    .S(\wait ), .clk(clock), .R(IRQ), .Q(s_r_ff_1_q));  // open: Qn, preset, reset, en
  S_R_Flip_Flop #(.trigger("falling")) s_r_ff_2 (
    .S(halt), .clk(clk_no_inhibit), .R(1'b0), .Q(s_r_ff_2_q));  // open: Qn, preset, reset, en
  S_R_Flip_Flop #(.trigger("falling")) s_r_ff_3 (
    .S(critical_fault), .clk(clk_no_inhibit), .R(1'b0), .Q(s_r_ff_3_q));  // open: Qn, preset, reset, en
  Counter #(.width(3), .max('h7), .trigger("falling")) counter_1 (
    .load(CUT), .D(3'b000), .count(not_1_out), .Q(phase), .clk(clk));  // open: carry, clr
  Decoder #(.select(3), .enable("false")) decoder_1 (
    .out0(decoder_1_out0), .out1(decoder_1_out1), .out2(decoder_1_out2), .out3(decoder_1_out3),
    .out4(decoder_1_out4), .out5(decoder_1_out5), .out6(decoder_1_out6), .out7(decoder_1_out7),
    .sel(br_abs_flags_d[2:0]));
  or or_1 (or_1_out, d_ff_1_q, s_r_ff_1_q, or_2_out);
  or or_2 (or_2_out, s_r_ff_2_q, s_r_ff_3_q);
  nor nor_1 (nor_1_out, phase[0], phase[1], phase[2]);
  D_Flip_Flop #(.trigger("falling")) d_ff_2 (
    .clk(clk), .D(d_ff_2_qn), .Qn(d_ff_2_qn), .en(CUT));  // open: Q, preset, reset
  Decoder #(.select(3), .disabled(0)) decoder_2 (
    .out0(r0DXa), .out1(r1DXa), .out2(r2DXa), .out3(r3DXa), .out4(r4DXa), .out5(r5DXa), .out6(r6DXa),
    .out7(fpDXa), .sel(rdX), .en(DXa));
  Pull_Resistor pull_resistor_1 (.node(bus0));
  Pull_Resistor pull_resistor_2 (.node(bus1));
  Multiplexer #(.width(16), .enable("false")) multiplexer_1 (
    .in0(busD), .in1(busDX), .out(multiplexer_1_out), .sel(r0DXa));
  and and_1 (r0_s_en, decoder_1_out0, r_latch);
  and and_2 (and_2_out, r_asrtD, decoder_1_out0);
  and and_3 (clk_no_inhibit, clock, not_2_out);
  not not_2 (not_2_out, or_1_out);
  Priority_Encoder #(.select(2)) priority_encoder_1 (
    .in0(1'b1), .in1(s_r_ff_1_q), .in2(s_r_ff_2_q), .in3(s_r_ff_3_q), .out(status));  // open: gs, en_out, en_in
  and and_4 (and_4_out, startup, clk);
  and and_5 (fetch, nor_1_out, d_ff_2_qn);
  Pull_Resistor pull_resistor_3 (.node(alu_asrtDX));
  Pull_Resistor pull_resistor_4 (.node(r_asrtDX));
  Pull_Resistor pull_resistor_5 (.node(DXa));
  Pull_Resistor pull_resistor_6 (.node(r_latchx));
  Multiplexer #(.width(16), .enable("false")) multiplexer_2 (
    .in0(busD), .in1(busDX), .out(multiplexer_2_out), .sel(r1DXa));
  Register #(.width(16), .trigger("falling")) register_2 (
    .D(multiplexer_1_out), .en(register_enable_1_out), .Q(R0), .clk(clk));  // open: clr
  Register #(.width(16), .trigger("falling")) register_3 (
    .D(multiplexer_2_out), .en(register_enable_2_out), .Q(R1), .clk(clk));  // open: clr
  register_enable register_enable_1 (.busDa(r0_s_en), .busDXa(r0_DX_en), .out(register_enable_1_out), .switcher(DXa));
  register_enable register_enable_2 (.busDa(r1_s_en), .busDXa(r1_DX_en), .out(register_enable_2_out), .switcher(DXa));
  and and_6 (r1_s_en, decoder_1_out1, r_latch);
  and and_7 (and_7_out, r_asrtD, decoder_1_out1);
  assign busD = and_2_out ? R0 : 16'bz;  // Controlled_Buffer controlled_buffer_1
  or or_3 (or_3_out, or_4_out, EXC);
  or or_4 (or_4_out, exc_trig_invalid_inst, exc_trig_pc, exc_trig_sp);
  not not_3 (not_3_out, clk_inhibit);
  and and_8 (clk, not_3_out, clk_no_inhibit);
  D_Flip_Flop #(.trigger("falling")) d_ff_3 (.clk(and_4_out), .D(CUT), .Qn(startup));  // open: Q, preset, en, reset
  Pull_Resistor pull_resistor_7 (.node(rdX));
  Multiplexer #(.width(16), .enable("false")) multiplexer_3 (
    .in0(busD), .in1(busDX), .out(multiplexer_3_out), .sel(r2DXa));
  Register #(.width(16), .trigger("falling")) register_4 (
    .D(multiplexer_3_out), .en(register_enable_3_out), .Q(R2), .clk(clk));  // open: clr
  register_enable register_enable_3 (.busDa(r2_s_en), .busDXa(r2_DX_en), .out(register_enable_3_out), .switcher(DXa));
  and and_9 (r2_s_en, decoder_1_out2, r_latch);
  and and_10 (and_10_out, r_asrtD, decoder_1_out2);
  assign busD = and_7_out ? R1 : 16'bz;  // Controlled_Buffer controlled_buffer_2
  assign busD = and_10_out ? R2 : 16'bz;  // Controlled_Buffer controlled_buffer_3
  and and_11 (and_11_out, or_4_out, EXC);
  Priority_Encoder priority_encoder_2 (
    .in1(exc_trig_sp), .in2(exc_trig_pc), .in3(exc_trig_invalid_inst), .in7(EXC),
    .out(priority_encoder_2_out), .gs(priority_encoder_2_gs));  // open: in0, in4, in5, in6, en_in, en_out
  Decoder #(.select(3), .enable("false")) decoder_3 (
    .out0(decoder_3_out0), .out1(decoder_3_out1), .out2(decoder_3_out2), .out3(decoder_3_out3),
    .out4(decoder_3_out4), .out5(decoder_3_out5), .out6(decoder_3_out6), .out7(decoder_3_out7), .sel(rdX));
  Multiplexer #(.width(16), .enable("false")) multiplexer_4 (
    .in0(busD), .in1(busDX), .out(multiplexer_4_out), .sel(r3DXa));
  Multiplexer #(.width(16), .enable("false")) multiplexer_5 (
    .in0(busD), .in1(busDX), .out(multiplexer_5_out), .sel(r4DXa));
  Register #(.width(16), .trigger("falling")) register_5 (
    .D(multiplexer_4_out), .en(register_enable_4_out), .Q(R3), .clk(clk));  // open: clr
  register_enable register_enable_4 (.busDa(r3_s_en), .busDXa(r3_DX_en), .out(register_enable_4_out), .switcher(DXa));
  and and_12 (r3_s_en, decoder_1_out3, r_latch);
  and and_13 (r4_s_en, decoder_1_out4, r_latch);
  and and_14 (and_14_out, r_asrtD, decoder_1_out4);
  and and_15 (and_15_out, r_asrtD, decoder_1_out3);
  assign busD = and_15_out ? R3 : 16'bz;  // Controlled_Buffer controlled_buffer_4
  and and_16 (and_16_out, or_3_out, exc_latch);
  or or_5 (or_5_out, rti, \int );
  or or_6 (latch_double_fault, and_11_out, and_16_out, or_5_out);
  Multiplexer #(.width(3), .enable("false")) multiplexer_6 (
    .in0(priority_encoder_2_out), .in1(3'b100), .out(multiplexer_6_out), .sel(latch_double_fault));
  Comparator #(.width(3), .mode("unsigned")) comparator_1 (
    .a(exc_internal_vec), .b(3'b111), .eq(comparator_1_eq));  // open: gt, lt
  assign bit_extender_1_out = {{13{1'b0}}, exc_internal_vec};  // Bit_Extender bit_extender_1
  assign bit_extender_2_out = {{10{1'b0}}, exc_vec_t};  // Bit_Extender bit_extender_2
  assign bit_extender_3_out = {{10{1'b0}}, exc_vec};  // Bit_Extender bit_extender_3
  assign bit_extender_4_out = {{13{1'b0}}, 3'b100};  // Bit_Extender bit_extender_4
  and and_17 (r0_DX_en, decoder_3_out0, r_latchx);
  and and_18 (r1_DX_en, decoder_3_out1, r_latchx);
  and and_19 (and_19_out, r_asrtDX, decoder_3_out0);
  and and_20 (and_20_out, r_asrtDX, decoder_3_out1);
  assign busDX = and_19_out ? R0 : 16'bz;  // Controlled_Buffer controlled_buffer_5
  Multiplexer #(.width(16), .enable("false")) multiplexer_7 (
    .in0(busD), .in1(busDX), .out(multiplexer_7_out), .sel(r5DXa));
  Register #(.width(16), .trigger("falling")) register_6 (
    .D(multiplexer_7_out), .en(register_enable_6_out), .Q(R5), .clk(clk));  // open: clr
  Register #(.width(16), .trigger("falling")) register_7 (
    .D(multiplexer_5_out), .en(register_enable_5_out), .Q(R4), .clk(clk));  // open: clr
  register_enable register_enable_5 (.busDa(r4_s_en), .busDXa(r4_DX_en), .out(register_enable_5_out), .switcher(DXa));
  register_enable register_enable_6 (.busDa(r5_s_en), .busDXa(r5_DX_en), .out(register_enable_6_out), .switcher(DXa));
  and and_21 (r5_s_en, decoder_1_out5, r_latch);
  and and_22 (and_22_out, r_asrtD, decoder_1_out5);
  assign busD = and_14_out ? R4 : 16'bz;  // Controlled_Buffer controlled_buffer_6
  Register #(.width(3), .trigger("falling")) register_8 (
    .D(multiplexer_6_out), .en(priority_encoder_2_gs), .Q(exc_internal_vec), .clk(clk_no_inhibit));  // open: clr
  Multiplexer #(.width(16), .enable("false")) multiplexer_8 (
    .in0(bit_extender_1_out), .in1(bit_extender_2_out), .out(multiplexer_8_out), .sel(comparator_1_eq));
  Multiplexer #(.width(16), .enable("false")) multiplexer_9 (
    .in0(bit_extender_3_out), .in1(bit_extender_4_out), .out(multiplexer_9_out), .sel(latch_double_fault));
  and and_23 (IAck, fetch, and_24_out);
  and and_24 (and_24_out, IRQ, PS[15]);
  or or_7 (latch_int, and_24_out, out_25);
  and and_25 (reset_exc, out_25, fetch);
  and and_26 (r2_DX_en, decoder_3_out2, r_latchx);
  and and_27 (r3_DX_en, decoder_3_out3, r_latchx);
  and and_28 (and_28_out, r_asrtDX, decoder_3_out3);
  and and_29 (and_29_out, r_asrtDX, decoder_3_out2);
  assign busDX = and_29_out ? R2 : 16'bz;  // Controlled_Buffer controlled_buffer_7
  assign busDX = and_20_out ? R1 : 16'bz;  // Controlled_Buffer controlled_buffer_8
  Multiplexer #(.width(16), .enable("false")) multiplexer_10 (
    .in0(busD), .in1(busDX), .out(multiplexer_10_out), .sel(r6DXa));
  Register #(.width(16), .trigger("falling")) register_9 (
    .D(multiplexer_10_out), .en(register_enable_7_out), .Q(R6), .clk(clk));  // open: clr
  register_enable register_enable_7 (.busDa(r6_s_en), .busDXa(r6_DX_en), .out(register_enable_7_out), .switcher(DXa));
  and and_30 (r6_s_en, decoder_1_out6, r_latch);
  and and_31 (and_31_out, r_asrtD, decoder_1_out6);
  assign busD = and_31_out ? R6 : 16'bz;  // Controlled_Buffer controlled_buffer_9
  assign busD = and_22_out ? R5 : 16'bz;  // Controlled_Buffer controlled_buffer_10
  S_R_Flip_Flop #(.trigger("falling")) s_r_ff_4 (
    .S(priority_encoder_2_gs), .clk(clk_no_inhibit), .R(reset_exc), .Q(exc_latch));  // open: Qn, preset, reset, en
  assign bit_extender_5_out = {{10{1'b0}}, int_vec};  // Bit_Extender bit_extender_5
  Multiplexer #(.width(16), .enable("false")) multiplexer_11 (
    .in0(multiplexer_8_out), .in1(multiplexer_9_out), .out(multiplexer_11_out), .sel(EXC));
  and and_32 (r5_DX_en, decoder_3_out5, r_latchx);
  and and_33 (r4_DX_en, decoder_3_out4, r_latchx);
  and and_34 (and_34_out, r_asrtDX, decoder_3_out5);
  and and_35 (and_35_out, r_asrtDX, decoder_3_out4);
  assign busDX = and_35_out ? R4 : 16'bz;  // Controlled_Buffer controlled_buffer_11
  assign busDX = and_28_out ? R3 : 16'bz;  // Controlled_Buffer controlled_buffer_12
  Multiplexer #(.width(16), .enable("false")) multiplexer_12 (
    .in0(busD), .in1(busDX), .out(multiplexer_12_out), .sel(fpDXa));
  Register #(.width(16), .trigger("falling")) register_10 (
    .D(multiplexer_12_out), .en(register_enable_8_out), .Q(FP), .clk(clk));  // open: clr
  register_enable register_enable_8 (.busDa(fp_s_en), .busDXa(fp_DX_en), .out(register_enable_8_out), .switcher(DXa));
  and and_36 (fp_s_en, decoder_1_out7, r_latch);
  and and_37 (and_37_out, r_asrtD, decoder_1_out7);
  assign busD = and_37_out ? FP : 16'bz;  // Controlled_Buffer controlled_buffer_13
  and and_38 (critical_fault, double_fault, priority_encoder_2_gs);
  or or_8 (out_25, priority_encoder_2_gs, exc_latch);
  Multiplexer #(.width(16), .enable("false")) multiplexer_13 (
    .in0(bit_extender_5_out), .in1(multiplexer_11_out), .out(multiplexer_13_out), .sel(out_25));
  assign or_9_out = multiplexer_13_out | 16'h8000;  // OR_Gate or_9, 16 bits wide
  and and_39 (fp_DX_en, decoder_3_out7, r_latchx);
  and and_40 (r6_DX_en, decoder_3_out6, r_latchx);
  and and_41 (and_41_out, r_asrtDX, decoder_3_out6);
  and and_42 (and_42_out, r_asrtDX, decoder_3_out7);
  assign busDX = and_41_out ? R6 : 16'bz;  // Controlled_Buffer controlled_buffer_14
  assign busDX = and_34_out ? R5 : 16'bz;  // Controlled_Buffer controlled_buffer_15
  Multiplexer #(.select(3), .width(16)) multiplexer_14 (
    .in0(R0), .in1(R1), .in2(R2), .in3(R3), .in4(R4), .in5(R5), .in6(R6), .in7(FP), .out(bus0), .sel(rs0),
    .en(r_asrt0));
  Multiplexer #(.select(3), .width(16)) multiplexer_15 (
    .in0(R0), .in1(R1), .in2(R2), .in3(R3), .in4(R4), .in5(R5), .in6(R6), .in7(FP), .out(bus1), .sel(rs1),
    .en(r_asrt1));
  Multiplexer #(.width(16), .enable("false")) multiplexer_16 (
    .in0(busD), .in1(or_9_out), .out(multiplexer_16_out), .sel(latch_int));
  Multiplexer #(.width(16), .enable("false")) multiplexer_17 (
    .in0(multiplexer_16_out), .in1(16'h8200), .out(fetched_instruction), .sel(startup));
  not not_4 (not_4_out, fetch);
  or or_10 (or_10_out, latch_int, startup);
  assign busDX = and_42_out ? FP : 16'bz;  // Controlled_Buffer controlled_buffer_16
  Pull_Resistor pull_resistor_8 (.node(busD));
  Register #(.width(16), .trigger("falling")) register_11 (
    .D(fetched_instruction), .en(fetch),
    .Q({register_11_q, br_rel_flags_d[3], alu_op_d1, alu_op_d0, imm6_d, br_abs_flags_d}), .clk(clk),
    .clr(and_43_out));
  and and_43 (and_43_out, fetch, not_4_out);
  D_Flip_Flop #(.trigger("falling")) d_ff_4 (
    .clk(clk), .D(or_10_out), .Q(virtual_instruction), .en(fetch));  // open: Qn, preset, reset
  Multiplexer #(.enable("false")) multiplexer_18 (
    .in0(br_rel_nop), .in1(virtual_instruction), .out(pc_inc_inhibit), .sel(out_25));
  assign bus0 = fp_asrt0 ? FP : 16'bz;  // Controlled_Buffer controlled_buffer_17
  assign bus1 = imm_asrt1 ? imm : 16'bz;  // Controlled_Buffer controlled_buffer_18
  assign busD = imm_asrtD ? imm : 16'bz;  // Controlled_Buffer controlled_buffer_19
  Decoder #(.select(3), .disabled(0), .enable("false")) decoder_4 (
    .out0(decoder_4_out0), .out1(_1op), .out2(decoder_4_out2), .out3(imm6), .out4(imm9),
    .out5(decoder_4_out5), .out6(decoder_4_out6), .out7(decoder_4_out7), .sel(register_11_q));
  Comparator #(.width(16), .mode("unsigned")) comparator_2 (
    .a(16'h8004), .b({register_11_q, br_rel_flags_d[3], alu_op_d1, alu_op_d0, imm6_d, br_abs_flags_d}),
    .eq(double_fault));  // open: gt, lt
  // Probe on sp_register_1_mon
  sp_register sp_register_1 (
    .In(busD), .plus_2(sp_inc), .en(sp_latch), .minus_2(sp_dec), .clk(clk), .Mon(sp_register_1_mon), .Out(SP));  // open: clr
  Demultiplexer #(.disabled(0), .enable("false")) demultiplexer_1 (
    .out0(demultiplexer_1_out0), .out1(shifts), .in(decoder_4_out0), .sel(br_rel_flags_d[3]));
  Demultiplexer #(.select(2), .disabled(0), .enable("false")) demultiplexer_2 (
    .out0(_2op), .out1(alu3_ind), .out2(mem2), .out3(alu2), .in(decoder_4_out2),
    .sel({br_rel_flags_d[3], alu_op_d1[2]}));
  Demultiplexer #(.disabled(0), .enable("false")) demultiplexer_3 (
    .out0(mem3), .out1(alu3), .in(decoder_4_out5), .sel(br_rel_flags_d[3]));
  assign bus0 = sp_asrt0 ? SP : 16'bz;  // Controlled_Buffer controlled_buffer_20
  Demultiplexer #(.disabled(0), .enable("false")) demultiplexer_4 (
    .out0(_0op), .out1(br_abs_d), .in(demultiplexer_1_out0), .sel(alu_op_d1[2]));
  Multiplexer #(.width(4), .enable("false")) multiplexer_19 (
    .in0({br_rel_flags_d[3], alu_op_d1}), .in1(br_abs_flags_d), .out(multiplexer_19_out), .sel(br_abs_d));
  branch_logic branch_logic_1 (.cccc(multiplexer_19_out), .CVZN(ps_flags), .go(branch_logic_1_go));
  assign bus0 = pc_asrt0 ? PC : 16'bz;  // Controlled_Buffer controlled_buffer_21
  // Probe on pc_register_1_mon
  and and_44 (and_44_out, pc_inc, not_8_out);
  pc_register pc_register_1 (
    .In(busD), .en(pc_latch), .plus_2(and_44_out), .Out(PC), .clk(clk), .Mon(pc_register_1_mon),
    .asrt_inc(and_45_out), .inverse_inc(out_25));  // open: clr
  and and_45 (and_45_out, jsr, pc_asrtD);
  and and_46 (br_abs_nop, br_abs_d, not_5_out);
  not not_5 (not_5_out, br_abs);
  and and_47 (br_abs, br_abs_d, branch_logic_1_go);
  and and_48 (and_48_out, decoder_4_out6, not_6_out);
  not not_6 (not_6_out, br_rel_n);
  and and_49 (br_rel_n, decoder_4_out6, branch_logic_1_go);
  and and_50 (and_50_out, decoder_4_out7, not_7_out);
  not not_7 (not_7_out, br_rel_p);
  and and_51 (br_rel_p, decoder_4_out7, branch_logic_1_go);
  not not_8 (not_8_out, pc_inc_inhibit);
  assign busD = sp_asrtD ? SP : 16'bz;  // Controlled_Buffer controlled_buffer_22
  Multiplexer #(.enable("false")) multiplexer_20 (
    .in0(and_52_out), .in1(PS[3]), .out(multiplexer_20_out), .sel(arith_carry));
  alu alu_1 (
    .A(bus0), .B(bus1), .Cin(multiplexer_20_out), .func(alu_func), .op_type(alu_op_type), .C(cout),
    .V(CVZN[2]), .Z(CVZN[1]), .N(CVZN[0]), .S(address), .shift_count(alu_op_d0), .mul_high(alu_1_mul_high));
  assign busD = pc_asrtD ? PC : 16'bz;  // Controlled_Buffer controlled_buffer_23
  or or_11 (or_11_out, alu_op_d1[1], alu_op_d1[2], br_rel_flags_d[3]);
  not not_9 (not_9_out, br_abs_flags_d[3]);
  or or_12 (br_rel_nop, and_48_out, and_50_out);
  and and_52 (and_52_out, mem, inc_address);
  assign busD = alu_asrtD ? address : 16'bz;  // Controlled_Buffer controlled_buffer_24
  and and_53 (\int , imm9, not_10_out);
  not not_10 (not_10_out, or_11_out);
  Decoder #(.select(2), .disabled(0)) decoder_5 (
    .out0(halt), .out1(\wait ), .out2(ei), .out3(di), .sel(br_abs_flags_d[1:0]), .en(and_54_out));
  and and_54 (and_54_out, and_55_out, not_11_out);
  and and_55 (and_55_out, br_abs_flags_d[2], not_9_out, _0op);
  not not_11 (not_11_out, out_25);
  or or_13 (or_13_out, shifts, alu2);
  assign bit_extender_6_out = {{7{1'b0}}, {alu_op_d0, imm6_d, br_abs_flags_d}};  // Bit_Extender bit_extender_6
  assign bit_extender_7_out = {{7{1'b1}}, {alu_op_d0, imm6_d, br_abs_flags_d}};  // Bit_Extender bit_extender_7
  Multiplexer #(.select(2), .width(16), .disabled(0), .enable("false")) multiplexer_21 (
    .in0(bit_extender_6_out), .in1(bit_extender_7_out), .in2(bit_extender_8_out), .in3(bit_extender_9_out),
    .out(multiplexer_21_out), .sel({imm6, imm_extend_negative}));
  assign bit_extender_8_out = {{10{1'b0}}, {alu_op_d0, imm6_d, br_abs_flags_d[3]}};  // Bit_Extender bit_extender_8
  assign bit_extender_9_out = {{10{1'b1}}, {alu_op_d0, imm6_d, br_abs_flags_d[3]}};  // Bit_Extender bit_extender_9
  assign busDX = alu_asrtDX ? alu_1_mul_high : 16'bz;  // Controlled_Buffer controlled_buffer_25
  LED led_1 (.in(PS[15]));
  LED led_2 (.in(clk));
  // Probe on ps_flags
  ps_register ps_register_1 (
    .flags({cout, CVZN}), .word(busD), .clk(clk), .out(PS), .out_flags(ps_flags),
    .latch_flags(ps_latch_flags), .latch_word(ps_latch_word), .ei(ei), .di(di));
  or or_14 (or_14_out, br_abs_nop, br_rel_nop);
  LED led_3 (.in(clk_no_inhibit));
  assign busD = ps_asrtD ? PS : 16'bz;  // Controlled_Buffer controlled_buffer_26
  or or_15 (or_15_out, br_abs_flags_d[1], br_abs_flags_d[2]);
  not not_12 (not_12_out, or_15_out);
  Priority_Encoder priority_encoder_3 (
    .in0(_0op), .in1(_1op), .in2(_2op), .in3(mem2), .in4(imm6), .in5(imm9), .in6(mem3),
    .in7(priority_encoder_4_gs), .out(priority_encoder_3_out));  // open: en_in, gs, en_out
  Priority_Encoder priority_encoder_4 (
    .in0(br_abs), .in1(or_13_out), .in2(alu3_ind), .in3(alu3), .in4(br_rel_p), .in5(br_rel_n),
    .in6(or_14_out), .in7(fetch), .out(priority_encoder_4_out), .gs(priority_encoder_4_gs));  // open: en_in, en_out
  or or_16 (or_16_out[0], alu3, alu3_ind);
  Decoder #(.disabled(0)) decoder_6 (.out0(jsr), .out1(rti), .sel(br_abs_flags_d[0]), .en(and_56_out));
  and and_56 (and_56_out, not_12_out, br_abs_flags_d[3], _0op);
  Multiplexer #(.select(3), .width(4), .disabled(0), .enable("false")) multiplexer_22 (
    .in0(br_abs_flags_d), .in1({alu_op_d0[0], imm6_d, br_abs_flags_d[3]}), .in2({alu_op_d1[0], alu_op_d0}),
    .in3({alu_op_d1[0], alu_op_d0}), .in4({br_rel_flags_d[3], alu_op_d1}),
    .in5({br_rel_flags_d[3], alu_op_d1}), .in6({br_rel_flags_d[3], alu_op_d1}), .in7(bit_extender_10_out),
    .out(multiplexer_22_out), .sel(priority_encoder_3_out));
  assign bit_extender_10_out = {{1{1'b0}}, priority_encoder_4_out};  // Bit_Extender bit_extender_10
  or or_17 (or_17_out, shifts, alu2, or_16_out[0]);
  Shifter #(.width(16)) shifter_1 (.in(multiplexer_21_out), .\dist (4'b0001), .out(shifter_1_out));
  Shifter #(.width(16)) shifter_2 (.in(multiplexer_21_out), .\dist (4'b0010), .out(shifter_2_out));
  Multiplexer #(.width(3), .enable("false")) multiplexer_23 (
    .in0(3'b001), .in1({shifts, alu2, or_16_out[0]}), .out(alu_op_type), .sel(or_17_out));
  Multiplexer #(.width(16), .disabled(0), .enable("false")) multiplexer_24 (
    .in0(multiplexer_21_out), .in1(shifter_1_out), .out(multiplexer_24_out), .sel(imm_shift));
  Multiplexer #(.width(16), .disabled(0), .enable("false")) multiplexer_25 (
    .in0(shifter_2_out), .in1(or_18_out), .out(multiplexer_25_out), .sel(phase[0]));
  assign or_18_out = shifter_2_out | 16'h2;  // OR_Gate or_18, 16 bits wide
  not not_13 (not_13_out, or_19_out);
  or or_19 (or_19_out, io_phase, clk_inhibit);
  assign busD = rd_wr_prime ? bus_control_1_to_bus : 16'bz;  // Controlled_Buffer controlled_buffer_27
  Multiplexer #(.width(16), .disabled(0), .enable("false")) multiplexer_26 (
    .in0(multiplexer_24_out), .in1(multiplexer_25_out), .out(imm), .sel(\int ));
  and and_57 (word, word_t, not_13_out);
  bus_control bus_control_1 (
    .sign_extend(sign_extend), .odd_address(address[0]), .word(word_t), .clk_no_inhibit(clk_no_inhibit),
    .from_bus(busD), .data_in(data_in), .inc_address(inc_address), .clk_inhibit(clk_inhibit),
    .data_out(data_out), .to_bus(bus_control_1_to_bus), .phase(io_phase));
  Comparator #(.width(32)) comparator_3 (.a({32{1'b0}}), .b(rom_1_data), .eq(comparator_3_eq));  // open: gt, lt
  and and_58 (exc_trig_sp, rom_1_data[29], busD[1]);
  and and_59 (exc_trig_pc, busD[1], rom_1_data[13]);
  ROM #(.addrWidth(10), .dataWidth(32)) rom_1 (
    .addr({phase, priority_encoder_3_out, multiplexer_22_out}), .data(rom_1_data));  // open: sel
  ROM #(.addrWidth(10), .dataWidth(32)) rom_2 (
    .addr({phase, priority_encoder_3_out, multiplexer_22_out}), .data(rom_2_data));  // open: sel
  or or_20 (or_20_out, _1op, alu3_ind);
  Multiplexer #(.width(3), .disabled(0), .enable("false")) multiplexer_27 (
    .in0(alu_op_d0), .in1(br_abs_flags_d[2:0]), .out(rs1), .sel(or_20_out));
  Multiplexer #(.width(3), .disabled(0), .enable("false")) multiplexer_28 (
    .in0({imm6_d, br_abs_flags_d[3]}), .in1(br_abs_flags_d[2:0]), .out(rs0), .sel(imm6));
  and and_60 (exc_trig_invalid_inst, comparator_3_eq, not_14_out);
  not not_14 (not_14_out, exc_latch);
  Multiplexer #(.width(32), .enable("false")) multiplexer_29 (
    .in0(rom_1_data), .in1(rom_2_data), .out(multiplexer_29_out), .sel(out_25));
  and and_61 (and_61_out, alu_op_d1[1], alu_op_d1[2], br_rel_flags_d[3]);
  Multiplexer #(.width(32), .enable("false")) multiplexer_30 (
    .in0(multiplexer_29_out), .in1(32'h80000000),
    .out({CUT, word_t, sp_latch, sp_inc, sp_dec, sp_asrtD, sp_asrt0, sign_extend, rd_wr_prime, r_latchx, r_latch, r_asrtDX, r_asrtD, r_asrt1, r_asrt0, ps_latch_word, ps_latch_flags, ps_asrtD, pc_latch, pc_inc, pc_asrtD, pc_asrt0, mem, imm_shift, imm_extend_negative, imm_asrtD, imm_asrt1, fp_asrt0, data_ins_prime, alu_asrtDX, alu_asrtD, DXa}),
    .sel(or_21_out));
  or or_21 (or_21_out, status[1], startup, and_62_out);
  and and_62 (and_62_out, latch_int, fetch);
  and and_63 (and_63_out, imm6, and_61_out);
  or or_22 (arith_carry, shifts, alu3);
  or or_23 (or_23_out, alu2, alu3_ind);
  Multiplexer #(.width(3), .enable("false")) multiplexer_31 (
    .in0(3'b101), .in1(3'b110), .out(multiplexer_31_out), .sel(and_63_out));
  Multiplexer #(.width(3), .enable("false")) multiplexer_32 (
    .in0(alu_op_d1), .in1(alu_op_d0), .out(multiplexer_32_out), .sel(or_23_out));
  or or_24 (or_24_out, or_23_out, arith_carry);
  Multiplexer #(.width(3), .enable("false")) multiplexer_33 (
    .in0(multiplexer_31_out), .in1(multiplexer_32_out), .out(alu_func), .sel(or_24_out));

  // Other names for the same wires on the sheet: data = data_ins_prime; read = rd_wr_prime;
  //   address_out[15:0] = address; busA[15:0] = address; CVZN[3] = cout; direct_exc_vec[5:0] = exc_vec;
  //   exc_trig_ext = EXC; exc_triggered = out_25; imm9_d[8:0] = {alu_op_d0, imm6_d, br_abs_flags_d};
  //   op_type_d0[3:0] = br_abs_flags_d; rd[2:0] = br_abs_flags_d[2:0]; rd_d[2:0] = br_abs_flags_d[2:0];
  //   imm6_d (some bits) = {alu_op_d0, br_abs_flags_d[3]};
  //   op_type_d1[3:0] = {alu_op_d0[0], imm6_d, br_abs_flags_d[3]}; rs0_d[2:0] = {imm6_d, br_abs_flags_d[3]};
  //   op_type_d2[3:0] = {alu_op_d1[0], alu_op_d0}; rs1_d[2:0] = alu_op_d0; shift_count_d[2:0] = alu_op_d0;
  //   br_rel_flags_d[2:0] = alu_op_d1; op_type_d3[3:0] = {br_rel_flags_d[3], alu_op_d1};
  //   XY[1:0] = {br_rel_flags_d[3], alu_op_d1[2]}; Y = alu_op_d1[2]; X = br_rel_flags_d[3]; pc_value[15:0] = PC;
  //   ps_value[15:0] = PS; cin = PS[3]; int_en = PS[15]; sp_value[15:0] = SP

  // Notes on the sheet:
  //   IRQ: pull=down
  //   clock: pull=down
  //   hold: pull=down
  //   EXC: pull=down
  //   data_in: pull=down
  //   0 - running
  //   1 - waiting
  //   2 - halted
  //   3 - fault
  //   2
  //   3
  //   1
  //   int, reset, rti
  //   Double fault: 1. Unrecoverable instruction
  //   2. Multiple exceptions on the same phase
  //   3. Mutiple exceptions across several phases
  //   SP
  //   Coco-de-Mer 16
  //   Designed by Nikolay Repin
  //   2023
  //   PС
  //   int, reset
  //   CVZN
  //   PS
  //   1, 3, 5, 7
  //   contents of rom_1 (hex, n*v repeats v):
  //   4*0 4*c0000000 4a000a08 52802208 ca000a08 d2802208 ce000208 e2800208 ca004208 d2810208 ca080208
  //   d2a00208 c0a01600 4a000a08 84200000 a0080000 80204000 80090000 80200800 80082000 a2040002 5*0
  //   80228002 13*0 80720007 0 c0a20208 80a20208 81a20208 c0a20200 80a20200 81a20200 c00a0208 800a0208 8*0
  //   c0a00338 c0a003b8 80a00238 80a002b8 81a00238 81a002b8 c0080338 c00803b8 80080238 800802b8 80200040
  //   802000c0 80228022 802280a2 80028020 800280a0 4a004208 40802220 ca000248 ca0002c8 a2000122 a20001a2
  //   4a000a08 4a000a08 8*0 c0a60208 80a60208 81a60208 c0a60200 80a60200 81a60200 c00e0208 800e0208 8*0
  //   c0802600 80228002 80068000 80268002 80002522 800025a2 80001000 c0801600 16*0 c0802600 d2810208 9*0
  //   80082000 60*0 4a000a08 c0810220 4*0 80002522 800025a2 120*0 40802220 127*0 c0810220
  //   contents of rom_2 (hex, n*v repeats v):
  //   4*0 4*c0000000 4a000a08 52800208 4a000a08 52800208 4e000208 42800208 4a004208 52800208 4a080208
  //   52800208 c0801600 4a000a08 4000000 80000 4000 80000 800 80000 2040002 5*0 20002 13*0 80120007 0
  //   c0821208 80821208 81821208 c0821200 80821200 81821200 c00a1208 800a1208 8*0 c0801338 c08013b8
  //   80801238 808012b8 81801238 818012b8 c0081338 c00813b8 80081238 800812b8 80001040 800010c0 80029022
  //   800290a2 80021020 800210a0 4a004208 40800220 4a000248 4a0002c8 82001122 820011a2 4a000a08 4a000a08
  //   8*0 c0861208 80861208 81861208 c0861200 80861200 81861200 c00e1208 800e1208 8*0 c0801600 80021002
  //   80061000 80061002 80001522 800015a2 80001000 c0800600 16*0 40800600 52800208 90001000 88001000
  //   90001000 80001000 90001000 88001000 90001000 88001000 0 80000 7*80001000 5*0 80001000 47*0 4a000a08
  //   40800220 90001000 90001000 0 0 522 5a2 48*0 90001000 8000000 9*0 90001000 60*0 40800220 80001000 4*0
  //   90001000 90001000 49*0 88001000 70*0 40800220 127*0 10000000 127*0 90001000
endmodule

module sp_register (
  input  [15:0] In,
  input  clr,
  input  clk,
  input  plus_2,
  input  en,
  input  minus_2,
  output [15:0] Out,
  output [15:0] Mon
);

  wire count, en_t;
  wire [15:0] incdec2_1_out, multiplexer_1_out;

  Register #(.width(16), .trigger("falling")) register_1 (
    .D(multiplexer_1_out), .en(en_t), .Q(Mon), .clk(clk), .clr(clr));
  Multiplexer #(.width(16), .disabled(0), .enable("false")) multiplexer_1 (
    .in0(In), .in1(incdec2_1_out), .out(multiplexer_1_out), .sel(count));
  or or_1 (count, plus_2, minus_2);
  or or_2 (en_t, count, en);
  incdec2 incdec2_1 (.in(Mon), .out(incdec2_1_out), .inc_dec_prime(plus_2));
  Multiplexer #(.width(16), .disabled(0), .enable("false")) multiplexer_2 (
    .in0(Mon), .in1(incdec2_1_out), .out(Out), .sel(minus_2));

  // Notes on the sheet:
  //   en: pull=up
  //   minus_2: pull=down
  //   clk: pull=down
  //   clr: pull=down
  //   plus_2: pull=down
endmodule

module pc_register (
  input  [15:0] In,
  input  clr,
  input  clk,
  input  en,
  input  plus_2,
  input  asrt_inc,
  input  inverse_inc,
  output [15:0] Out,
  output [15:0] Mon
);

  wire en_t, not_1_out;
  wire [15:0] incdec2_1_out, multiplexer_1_out;

  Multiplexer #(.width(16), .disabled(0), .enable("false")) multiplexer_1 (
    .in0(In), .in1(incdec2_1_out), .out(multiplexer_1_out), .sel(plus_2));
  Register #(.width(16), .trigger("falling")) register_1 (
    .D(multiplexer_1_out), .en(en_t), .Q(Mon), .clk(clk), .clr(clr));
  or or_1 (en_t, plus_2, en);
  incdec2 incdec2_1 (.in(Mon), .out(incdec2_1_out), .inc_dec_prime(not_1_out));
  not not_1 (not_1_out, inverse_inc);
  Multiplexer #(.width(16), .disabled(0), .enable("false")) multiplexer_2 (
    .in0(Mon), .in1(incdec2_1_out), .out(Out), .sel(asrt_inc));

  // Other names for the same wires on the sheet: count = plus_2

  // Notes on the sheet:
  //   asrt_inc: pull=down
  //   en: pull=up
  //   inverse_inc: pull=down
  //   clr: pull=down
  //   clk: pull=down
  //   plus_2: pull=down
endmodule

module ps_register (
  input  [3:0] flags,
  input  [15:0] word,
  input  clk,
  input  latch_word,
  input  latch_flags,
  input  ei,
  input  di,
  output [3:0] out_flags,
  output [15:0] out
);

  wire or_1_out, or_3_out, set_int_flag;
  wire [15:0] multiplexer_1_out, multiplexer_2_out;

  Multiplexer #(.width(16), .enable("false")) multiplexer_1 (
    .in0({out[15:4], flags}), .in1({ei, out[14:0]}), .out(multiplexer_1_out), .sel(set_int_flag));
  Multiplexer #(.width(16), .enable("false")) multiplexer_2 (
    .in0(multiplexer_1_out), .in1(word), .out(multiplexer_2_out), .sel(latch_word));
  or or_1 (or_1_out, latch_word, latch_flags);
  or or_2 (set_int_flag, ei, di);
  Register #(.width(16), .trigger("falling")) register_1 (
    .D(multiplexer_2_out), .en(or_3_out), .Q(out), .clk(clk));  // open: clr
  or or_3 (or_3_out, or_1_out, set_int_flag);
  Bit_Extender #(.in_width(16), .out_width(4)) bit_extender_1 (.in(out), .out(out_flags));

  // Notes on the sheet:
  //   ei: pull=down
  //   clk: pull=down
  //   latch_word: pull=down
  //   di: pull=down
  //   flags: pull=down
  //   latch_flags: pull=down
  //   word: pull=down
endmodule

module incdec2 (
  input  [15:0] in,
  input  inc_dec_prime,
  output [15:0] out
);

  wire [15:0] multiplexer_1_out;

  Multiplexer #(.width(16), .enable("false")) multiplexer_1 (
    .in0(16'hfffe), .in1(16'h2), .out(multiplexer_1_out), .sel(inc_dec_prime));
  Adder #(.width(16)) adder_1 (.a(in), .b(multiplexer_1_out), .out(out));  // open: cin, cout

  // Notes on the sheet:
  //   inc_dec_prime: pull=up
endmodule

module bus_control (
  input  sign_extend,
  input  odd_address,
  input  word,
  input  clk_no_inhibit,
  input  [15:0] from_bus,
  input  [15:0] data_in,
  output inc_address,
  output clk_inhibit,
  output phase,
  output [15:0] data_out,
  output [15:0] to_bus
);

  wire and_1_out;
  wire [7:0] bit_extender_1_out, register_1_q;
  wire [15:0] bytes_swap_1_out, make_byte_2_out, multiplexer_1_out, multiplexer_3_out, multiplexer_5_out,
       n2s_compliment_1_out;

  Bit_Extender #(.in_width(16), .out_width(8)) bit_extender_1 (.in(data_in), .out(bit_extender_1_out));
  and and_1 (and_1_out, clk_inhibit, clk_no_inhibit);
  Register #(.trigger("falling")) register_1 (
    .D(bit_extender_1_out), .Q(register_1_q), .clk(and_1_out));  // open: en, clr
  and and_2 (clk_inhibit, odd_address, word);
  make_byte make_byte_1 ();  // open: In, Out
  Multiplexer #(.width(16), .disabled(0), .enable("false")) multiplexer_1 (
    .in0(from_bus), .in1(bytes_swap_1_out), .out(multiplexer_1_out), .sel(inc_address));
  bytes_swap bytes_swap_1 (.In(from_bus), .Out(bytes_swap_1_out));
  make_byte make_byte_2 (.In(data_in), .Out(make_byte_2_out));
  _2s_compliment u_2s_compliment_1 (.In(data_in), .Out(n2s_compliment_1_out));
  D_Flip_Flop #(.trigger("falling")) d_ff_1 (
    .clk(clk_no_inhibit), .D(clk_inhibit), .Q(inc_address));  // open: Qn, preset, en, reset
  Multiplexer #(.width(16), .disabled(0), .enable("false")) multiplexer_2 (
    .in0(from_bus), .in1(multiplexer_1_out), .out(data_out), .sel(word));
  Multiplexer #(.width(16), .disabled(0), .enable("false")) multiplexer_3 (
    .in0(make_byte_2_out), .in1(n2s_compliment_1_out), .out(multiplexer_3_out), .sel(sign_extend));
  Multiplexer #(.width(16), .disabled(0), .enable("false")) multiplexer_4 (
    .in0(multiplexer_3_out), .in1(multiplexer_5_out), .out(to_bus), .sel(word));
  Multiplexer #(.width(16), .disabled(0), .enable("false")) multiplexer_5 (
    .in0(data_in), .in1({bit_extender_1_out, register_1_q}), .out(multiplexer_5_out), .sel(inc_address));

  assign phase = inc_address;

  // Other names for the same wires on the sheet: odd = odd_address

  // Notes on the sheet:
  //   data_in: pull=down
endmodule

module alu (
  input  [15:0] A,
  input  [15:0] B,
  input  Cin,
  input  [2:0] func,
  input  [2:0] op_type,
  input  [2:0] shift_count,
  output C,
  output V,
  output Z,
  output N,
  output [15:0] mul_high,
  output [15:0] S
);

  wire adc, add, adder_c, adder_carry, adder_v, \and , and_3_out, and_4_out, and_5_out, and_6_out, bic, mul,
       multiplexer_5_out, multiplexer_6_out, neg, \not , not_6_out, \or , or_2_out, or_3_out, rcl, rcr, rol,
       ror, sbc, scl, shifter_c, shl, shr, shra, sub, sxt, \xor ;
  wire [1:0] encoded_type;
  wire [15:0] adder_out, and_1_out, and_2_out, logic_out, make_byte_1_out, multiplexer_1_out,
       multiplexer_2_out, multiply_1_low_bits, n2s_compliment_1_out, not_1_out, not_2_out, not_3_out,
       not_4_out, or_1_out, shifter_out, unary_out, xor_1_out;

  Decoder #(.select(3), .disabled(0)) decoder_1 (
    .out0(\and ), .out1(\or ), .out2(\xor ), .out3(bic), .out4(add), .out5(adc), .out6(sub), .out7(sbc),
    .sel(func), .en(op_type[0]));
  Decoder #(.select(3), .disabled(0)) decoder_2 (
    .out0(neg), .out1(\not ), .out2(sxt), .out3(scl), .out4(mul), .sel(func), .en(op_type[1]));  // open: out5, out6, out7
  Decoder #(.select(3), .disabled(0)) decoder_3 (
    .out0(shl), .out1(shr), .out2(shra), .out3(rol), .out4(ror), .out5(rcl), .out6(rcr), .sel(func),
    .en(op_type[2]));  // open: out7
  _2s_compliment u_2s_compliment_1 (.In(A), .Out(n2s_compliment_1_out));
  make_byte make_byte_1 (.In(A), .Out(make_byte_1_out));
  assign and_1_out = A & B;  // AND_Gate and_1, 16 bits wide
  assign or_1_out = A | B;  // OR_Gate or_1, 16 bits wide
  assign xor_1_out = A ^ B;  // XOR_Gate xor_1, 16 bits wide
  assign and_2_out = A & not_1_out;  // AND_Gate and_2, 16 bits wide
  assign not_1_out = ~B;  // NOT_Gate not_1, 16 bits wide
  Multiplexer #(.width(16), .enable("false")) multiplexer_1 (
    .in0(A), .in1(not_2_out), .out(multiplexer_1_out), .sel(neg));
  assign not_2_out = ~A;  // NOT_Gate not_2, 16 bits wide
  Multiplexer #(.width(16), .enable("false")) multiplexer_2 (
    .in0(B), .in1(not_3_out), .out(multiplexer_2_out), .sel(or_2_out));
  assign not_3_out = ~B;  // NOT_Gate not_3, 16 bits wide
  or or_2 (or_2_out, sub, sbc);
  assign not_4_out = ~A;  // NOT_Gate not_4, 16 bits wide
  multiply multiply_1 (.A(A), .B(B), .low_bits(multiply_1_low_bits), .high_bits(mul_high));  // open: carry_bit
  barrel_shifter barrel_shifter_1 (
    .In(A), .cin(Cin), .shift_type(func), .distance(shift_count), .Out(shifter_out), .cout(shifter_c));
  adder16 adder16_1 (
    .A(multiplexer_1_out), .B(multiplexer_2_out), .S(adder_out), .Cin(adder_carry), .Cout(adder_c),
    .V(adder_v));
  Multiplexer #(.select(3), .width(16), .enable("false")) multiplexer_3 (
    .in0(adder_out), .in1(not_4_out), .in2(n2s_compliment_1_out), .in3(make_byte_1_out),
    .in4(multiply_1_low_bits), .out(unary_out), .sel(func));  // open: in5, in6, in7
  Multiplexer #(.select(2), .width(16), .enable("false")) multiplexer_4 (
    .in0(and_1_out), .in1(or_1_out), .in2(xor_1_out), .in3(and_2_out), .out(logic_out), .sel(func[1:0]));
  // NOT_Gate not_5 is placed but not wired
  and and_3 (and_3_out, sbc, Cin);
  or or_3 (or_3_out, and_3_out, and_4_out);
  and and_4 (and_4_out, Cin, adc);
  or or_4 (adder_carry, or_3_out, neg, sub);
  not not_6 (not_6_out, func[2]);
  Multiplexer #(.enable("false")) multiplexer_5 (.in0(1'b0), .in1(adder_c), .out(multiplexer_5_out), .sel(neg));
  Multiplexer #(.enable("false")) multiplexer_6 (.in0(1'b0), .in1(adder_v), .out(multiplexer_6_out), .sel(neg));
  and and_5 (and_5_out, op_type[0], not_6_out);
  and and_6 (and_6_out, func[2], op_type[0]);
  Multiplexer #(.select(2), .width(16), .enable("false")) multiplexer_7 (
    .in0(logic_out), .in1(adder_out), .in2(unary_out), .in3(shifter_out), .out({N, S[14:0]}),
    .sel(encoded_type));
  Multiplexer #(.select(2), .enable("false")) multiplexer_8 (
    .in0(1'b0), .in1(adder_c), .in2(multiplexer_5_out), .in3(shifter_c), .out(C), .sel(encoded_type));
  Multiplexer #(.select(2), .enable("false")) multiplexer_9 (
    .in0(1'b0), .in1(adder_v), .in2(multiplexer_6_out), .in3(1'b0), .out(V), .sel(encoded_type));
  Priority_Encoder #(.select(2), .disabled(0)) priority_encoder_1 (
    .in0(and_5_out), .in1(and_6_out), .in2(op_type[1]), .in3(op_type[2]), .out(encoded_type));  // open: gs, en_out, en_in
  Pull_Resistor pull_resistor_1 (.node(encoded_type));
  // Probe on {N, S[14:0]}
  // NOT_Gate not_7 is placed but not wired
  zero16 zero16_1 (.in({N, S[14:0]}), .zero(Z));
  // NOT_Gate not_8 is placed but not wired

  assign S[15] = N;

  // Other names for the same wires on the sheet: _3op = op_type[0]; _2op = op_type[1]; shifts = op_type[2]

  // Notes on the sheet:
  //   shift_count: pull=down
  //   A: pull=down
  //   B: pull=down
  //   op_type: pull=down
  //   func: pull=down
  //   Cin: pull=down
endmodule

module barrel_shifter (
  input  [15:0] In,
  input  cin,
  input  [2:0] shift_type,
  input  [2:0] distance,
  output [15:0] Out,
  output cout
);

  wire [4:0] adder_1_out, bit_extender_1_out;
  wire [15:0] shifter_4_out, shifter_5_out;
  wire [16:0] shifter_1_out, shifter_2_out, shifter_3_out, shifter_6_out, shifter_7_out;

  assign bit_extender_1_out = {{2{1'b0}}, distance};  // Bit_Extender bit_extender_1
  Adder #(.width(5)) adder_1 (.a(bit_extender_1_out), .b(5'b00001), .out(adder_1_out));  // open: cin, cout
  Shifter #(.width(17)) shifter_1 (.in({{2{In[15]}}, In[14:0]}), .\dist (adder_1_out), .out(shifter_1_out));
  Shifter #(.width(17), .shift("lr")) shifter_2 (.in({In, In[0]}), .\dist (adder_1_out), .out(shifter_2_out));
  Shifter #(.width(17), .shift("ar")) shifter_3 (.in({In, In[0]}), .\dist (adder_1_out), .out(shifter_3_out));
  Shifter #(.width(16), .shift("rl")) shifter_4 (.in(In), .\dist (adder_1_out[3:0]), .out(shifter_4_out));
  Shifter #(.width(16), .shift("rr")) shifter_5 (.in(In), .\dist (adder_1_out[3:0]), .out(shifter_5_out));
  Shifter #(.width(17), .shift("rl")) shifter_6 (.in({cin, In}), .\dist (adder_1_out), .out(shifter_6_out));
  Shifter #(.width(17), .shift("rr")) shifter_7 (.in({In, cin}), .\dist (adder_1_out), .out(shifter_7_out));
  Multiplexer #(.select(3), .width(16), .enable("false")) multiplexer_1 (
    .in0(shifter_1_out[15:0]), .in1(shifter_2_out[16:1]), .in2(shifter_3_out[16:1]), .in3(shifter_4_out),
    .in4(shifter_5_out), .in5(shifter_6_out[15:0]), .in6(shifter_7_out[16:1]), .out(Out), .sel(shift_type));  // open: in7
  Multiplexer #(.select(3), .enable("false")) multiplexer_2 (
    .in0(shifter_1_out[16]), .in1(shifter_2_out[0]), .in2(shifter_3_out[0]), .in3(shifter_4_out[0]),
    .in4(shifter_5_out[15]), .in5(shifter_6_out[16]), .in6(shifter_7_out[0]), .out(cout), .sel(shift_type));  // open: in7

  // Other names for the same wires on the sheet: value[15:0] = In; type[2:0] = shift_type

  // Notes on the sheet:
  //   In: pull=down
  //   cin: pull=down
  //   distance: pull=down
  //   shift_type: pull=down
  //   shl
  //   shr
  //   shra
  //   rol
  //   ror
  //   rcl
  //   rcr
endmodule

module adder16 (
  input  Cin,
  input  [15:0] A,
  input  [15:0] B,
  output [15:0] S,
  output Cout,
  output V
);

  wire [15:0] and_1_out, and_2_out, and_3_out;
  wire [15:1] or_1_out;

  // Probe on A
  // Probe on B
  assign S = A ^ {or_1_out, Cin} ^ B;  // XOR_Gate xor_1, 16 bits wide
  assign and_1_out = B & A;  // AND_Gate and_1, 16 bits wide
  assign and_2_out = B & {or_1_out, Cin};  // AND_Gate and_2, 16 bits wide
  assign and_3_out = A & {or_1_out, Cin};  // AND_Gate and_3, 16 bits wide
  assign {Cout, or_1_out} = and_1_out | and_2_out | and_3_out;  // OR_Gate or_1, 16 bits wide
  // Probe on S
  xor xor_2 (V, or_1_out[15], Cout);

  // Notes on the sheet:
  //   Cin: pull=down
  //   A: pull=down
  //   B: pull=down
endmodule

module branch_logic (
  input  [3:0] cccc,
  input  [3:0] CVZN,
  output go
);

  wire and_1_out, and_2_out, and_3_out, and_4_out, and_5_out, and_6_out, and_7_out, decoder_1_out0,
       decoder_1_out1, decoder_1_out2, decoder_1_out3, decoder_2_out0, decoder_2_out1, decoder_2_out2,
       decoder_2_out3, not_1_out, not_2_out, or_1_out, xnor_1_out;

  not not_1 (not_1_out, cccc[3]);
  Decoder #(.select(2), .disabled(0)) decoder_1 (
    .out0(decoder_1_out0), .out1(decoder_1_out1), .out2(decoder_1_out2), .out3(decoder_1_out3),
    .sel(cccc[2:1]), .en(not_1_out));
  and and_1 (and_1_out, decoder_1_out0, CVZN[1]);
  and and_2 (and_2_out, decoder_1_out1, CVZN[3]);
  and and_3 (and_3_out, decoder_1_out2, CVZN[0]);
  and and_4 (and_4_out, decoder_1_out3, CVZN[2]);
  not not_2 (not_2_out, CVZN[1]);
  xnor xnor_1 (xnor_1_out, CVZN[0], CVZN[2]);
  Decoder #(.select(2), .disabled(0)) decoder_2 (
    .out0(decoder_2_out0), .out1(decoder_2_out1), .out2(decoder_2_out2), .out3(decoder_2_out3),
    .sel(cccc[2:1]), .en(cccc[3]));
  and and_5 (and_5_out, decoder_2_out0, not_2_out, CVZN[3]);
  and and_6 (and_6_out, xnor_1_out, decoder_2_out1);
  and and_7 (and_7_out, not_2_out, xnor_1_out, decoder_2_out2);
  or or_1 (or_1_out, and_1_out, and_2_out, and_3_out, and_4_out, and_5_out, and_6_out, and_7_out, decoder_2_out3);
  xor xor_1 (go, cccc[0], or_1_out);

  // Notes on the sheet:
  //   N
  //   Z
  //   V
  //   C
  //   EQ
  //   HS/CS
  //   MI
  //   VS
  //   N=V
  //   Z'
  //   HI
  //   GE
  //   GT
  //   <always>
endmodule

module zero16 (
  input  [15:0] in,
  output zero
);

  wire nor_1_out, nor_2_out;

  nor nor_1 (nor_1_out, in[0], in[1], in[2], in[3], in[4], in[5], in[6], in[7]);
  nor nor_2 (nor_2_out, in[8], in[9], in[10], in[11], in[12], in[13], in[14], in[15]);
  and and_1 (zero, nor_1_out, nor_2_out);
endmodule

module _2s_compliment (
  input  [15:0] In,
  output [15:0] Out
);

  wire [7:0] bit_extender_1_out;

  Bit_Extender #(.in_width(16), .out_width(8)) bit_extender_1 (.in(In), .out(bit_extender_1_out));
  assign Out = {{8{bit_extender_1_out[7]}}, bit_extender_1_out};  // Bit_Extender bit_extender_2
endmodule

module make_byte (
  input  [15:0] In,
  output [15:0] Out
);

  wire [7:0] bit_extender_1_out;

  Bit_Extender #(.in_width(16), .out_width(8)) bit_extender_1 (.in(In), .out(bit_extender_1_out));
  assign Out = {{8{1'b0}}, bit_extender_1_out};  // Bit_Extender bit_extender_2
endmodule

module bytes_swap (
  input  [15:0] In,
  output [15:0] Out
);


  assign Out = {In[7:0], In[15:8]};
endmodule
