// Logisim project beta-cdm16m.circ as structural Verilog: 16 circuits, main circuit cdm16
module cdm16 (
  input  [15:0] data_in,
  input  EXC,
  input  [5:0] exc_vec,
  input  IRQ,
  input  [5:0] int_vec,
  input  clock,
  input  hold,
  output [15:0] SP,
  output [15:0] PC,
  output [15:0] PS,
  output [15:0] R0,
  output [15:0] R1,
  output [15:0] R2,
  output [15:0] R3,
  output [15:0] R4,
  output [15:0] address,
  output mem,
  output [15:0] R5,
  output data_ins_prime,
  output rd_wr_prime,
  output [15:0] R6,
  output [15:0] FP,
  output word,
  output [15:0] data_out,
  output [1:0] status,
  output IAck,
  output fetch
);

  wire _0op, _1op, _2op, alu2, alu3, alu3_ind, alu_asrtD, and_1_out, and_2_out, and_4_out, and_6_out,
       and_7_out, and_9_out, and_10_out, and_11_out, and_12_out, and_13_out, and_14_out, and_15_out,
       and_16_out, and_17_out, and_18_out, and_20_out, and_22_out, and_23_out, and_24_out, and_25_out,
       and_27_out, and_28_out, and_29_out, and_32_out, and_34_out, and_36_out, and_38_out, and_39_out,
       and_40_out, and_45_out, and_46_out, and_47_out, arith_carry, br_abs, br_abs_d, br_abs_nop, br_rel_n,
       br_rel_nop, br_rel_p, branch_logic_1_go, clk, clk_inhibit, clk_no_inhibit, comparator_1_eq,
       comparator_3_eq, cout, critical_fault, CUT, d_ff_1_q, d_ff_2_qn, decoder_1_out0, decoder_1_out1,
       decoder_1_out2, decoder_1_out3, decoder_1_out4, decoder_1_out5, decoder_1_out6, decoder_1_out7,
       decoder_2_out0, decoder_2_out2, decoder_2_out5, decoder_2_out6, decoder_2_out7, demultiplexer_1_out0,
       di, double_fault, ei, exc_latch, exc_trig_invalid_inst, exc_trig_pc, exc_trig_sp, exc_triggered,
       fp_asrt0, halt, imm6, imm9, imm_asrt1, imm_asrtD, imm_extend_negative, imm_shift, inc_address, \int ,
       io_phase, jsr, latch_double_fault, latch_int, mdu_exc, mem2, mem3, multiplexer_13_out, nor_1_out,
       not_1_out, not_2_out, not_3_out, not_4_out, not_5_out, not_6_out, not_7_out, not_8_out, not_9_out,
       not_10_out, not_11_out, not_12_out, not_13_out, not_14_out, or_1_out, or_2_out, or_3_out, or_4_out,
       or_5_out, or_10_out, or_11_out, or_13_out, or_14_out, or_15_out, or_17_out, or_19_out, or_20_out,
       or_21_out, or_23_out, or_24_out, pc_asrt0, pc_asrtD, pc_inc, pc_inc_inhibit, pc_latch,
       priority_encoder_2_gs, priority_encoder_4_gs, ps_asrtD, ps_latch_flags, ps_latch_word, r_asrt0,
       r_asrt1, r_asrtD, r_latch, reset_exc, rti, s_r_ff_1_q, s_r_ff_2_q, s_r_ff_3_q, shifts, sign_extend,
       sp_asrt0, sp_asrtD, sp_dec, sp_inc, sp_latch, startup, virtual_instruction, \wait , word_t,
       x_mdu_asrtD, x_mdu_phase, x_mdu_phase_part, x_mdu_sigswap;
  wire [0:0] or_16_out;
  wire [2:0] alu_func, alu_op_d0, alu_op_d1, alu_op_type, CVZN, exc_internal_vec, multiplexer_1_out,
       multiplexer_2_out, multiplexer_24_out, multiplexer_25_out, phase, priority_encoder_2_out,
       priority_encoder_3_out, priority_encoder_4_out, rs0, rs1;
  wire [2:1] imm6_d;
  wire [3:0] bit_extender_10_out, br_abs_flags_d, multiplexer_12_out, multiplexer_15_out, ps_flags;
  wire [3:3] br_rel_flags_d;
  wire [5:0] exc_vec_t;
  wire [15:0] bit_extender_1_out, bit_extender_2_out, bit_extender_3_out, bit_extender_4_out,
       bit_extender_5_out, bit_extender_6_out, bit_extender_7_out, bit_extender_8_out, bit_extender_9_out,
       bus0, bus1, bus_control_1_to_bus, busD, fetched_instruction, imm, mdu_out, multiplexer_3_out,
       multiplexer_4_out, multiplexer_5_out, multiplexer_6_out, multiplexer_9_out, multiplexer_14_out,
       multiplexer_17_out, multiplexer_18_out, or_9_out, or_18_out, pc_register_1_mon, shifter_1_out,
       shifter_2_out, sp_register_1_mon;
  wire [15:13] register_11_q;
  wire [29:0] multiplexer_22_out, rom_1_data, rom_2_data;

  not not_1 (not_1_out, CUT);
  Register #(.width(6), .trigger("falling")) register_1 (
    .D(exc_vec), .en(EXC), .Q(exc_vec_t), .clk(clk_no_inhibit));  // open: clr
  D_Flip_Flop #(.trigger("low")) d_ff_1 (.clk(clock), .D(hold), .Q(d_ff_1_q));  // open: Qn, preset, en, reset
  S_R_Flip_Flop #(.trigger("falling")) s_r_ff_1 (
    .S(\wait ), .clk(clock), .R(IRQ), .Q(s_r_ff_1_q));  // open: Qn, preset, reset, en
  S_R_Flip_Flop #(.trigger("falling")) s_r_ff_2 (
    .S(halt), .clk(clk_no_inhibit), .R(1'b0), .Q(s_r_ff_2_q));  // open: Qn, preset, reset, en
  S_R_Flip_Flop #(.trigger("falling")) s_r_ff_3 (
    .S(critical_fault), .clk(clk_no_inhibit), .R(1'b0), .Q(s_r_ff_3_q));  // open: Qn, preset, reset, en
  Counter #(.width(3), .max('h7), .trigger("falling")) counter_1 (
    .load(CUT), .D(3'b000), .count(not_1_out), .Q(phase), .clk(clk));  // open: carry, clr
  Decoder #(.select(3), .enable("false")) decoder_1 (
    .out0(decoder_1_out0), .out1(decoder_1_out1), .out2(decoder_1_out2), .out3(decoder_1_out3),
    .out4(decoder_1_out4), .out5(decoder_1_out5), .out6(decoder_1_out6), .out7(decoder_1_out7),
    .sel(multiplexer_1_out));
  Multiplexer #(.width(3), .enable("false")) multiplexer_1 (
    .in0(br_abs_flags_d[2:0]), .in1(rs0), .out(multiplexer_1_out), .sel(x_mdu_sigswap));
  or or_1 (or_1_out, d_ff_1_q, s_r_ff_1_q, or_2_out);
  or or_2 (or_2_out, s_r_ff_2_q, s_r_ff_3_q);
  nor nor_1 (nor_1_out, phase[0], phase[1], phase[2]);
  D_Flip_Flop #(.trigger("falling")) d_ff_2 (
    .clk(clk), .D(d_ff_2_qn), .Qn(d_ff_2_qn), .en(CUT));  // open: Q, preset, reset
  Pull_Resistor pull_resistor_1 (.node(bus0));
  Pull_Resistor pull_resistor_2 (.node(bus1));
  Pull_Resistor pull_resistor_3 (.node(busD));
  and and_1 (and_1_out, decoder_1_out0, r_latch);
  and and_2 (and_2_out, r_asrtD, decoder_1_out0);
  and and_3 (clk_no_inhibit, clock, not_2_out);
  not not_2 (not_2_out, or_1_out);
  Priority_Encoder #(.select(2)) priority_encoder_1 (
    .in0(1'b1), .in1(s_r_ff_1_q), .in2(s_r_ff_2_q), .in3(s_r_ff_3_q), .out(status));  // open: gs, en_out, en_in
  and and_4 (and_4_out, startup, clk);
  and and_5 (fetch, nor_1_out, d_ff_2_qn);
  Register #(.width(16), .trigger("falling")) register_2 (.D(busD), .en(and_1_out), .Q(R0), .clk(clk));  // open: clr
  Register #(.width(16), .trigger("falling")) register_3 (.D(busD), .en(and_6_out), .Q(R1), .clk(clk));  // open: clr
  and and_6 (and_6_out, decoder_1_out1, r_latch);
  and and_7 (and_7_out, r_asrtD, decoder_1_out1);
  assign busD = and_2_out ? R0 : 16'bz;  // Controlled_Buffer controlled_buffer_1
  or or_3 (or_3_out, or_4_out, EXC);
  or or_4 (or_4_out, mdu_exc, exc_trig_invalid_inst, exc_trig_pc, exc_trig_sp);
  not not_3 (not_3_out, clk_inhibit);
  and and_8 (clk, not_3_out, clk_no_inhibit);
  D_Flip_Flop #(.trigger("falling")) d_ff_3 (.clk(and_4_out), .D(CUT), .Qn(startup));  // open: Q, preset, en, reset
  Register #(.width(16), .trigger("falling")) register_4 (.D(busD), .en(and_9_out), .Q(R2), .clk(clk));  // open: clr
  and and_9 (and_9_out, decoder_1_out2, r_latch);
  and and_10 (and_10_out, r_asrtD, decoder_1_out2);
  assign busD = and_10_out ? R2 : 16'bz;  // Controlled_Buffer controlled_buffer_2
  assign busD = and_7_out ? R1 : 16'bz;  // Controlled_Buffer controlled_buffer_3
  and and_11 (and_11_out, or_4_out, EXC);
  Priority_Encoder priority_encoder_2 (
    .in1(exc_trig_sp), .in2(exc_trig_pc), .in3(exc_trig_invalid_inst), .in6(mdu_exc), .in7(EXC),
    .out(priority_encoder_2_out), .gs(priority_encoder_2_gs));  // open: in0, in4, in5, en_in, en_out
  Register #(.width(16), .trigger("falling")) register_5 (.D(busD), .en(and_12_out), .Q(R3), .clk(clk));  // open: clr
  and and_12 (and_12_out, decoder_1_out3, r_latch);
  and and_13 (and_13_out, decoder_1_out4, r_latch);
  and and_14 (and_14_out, r_asrtD, decoder_1_out3);
  and and_15 (and_15_out, r_asrtD, decoder_1_out4);
  assign busD = and_14_out ? R3 : 16'bz;  // Controlled_Buffer controlled_buffer_4
  or or_5 (or_5_out, rti, \int );
  and and_16 (and_16_out, or_3_out, exc_latch);
  or or_6 (latch_double_fault, and_11_out, and_16_out, or_5_out);
  Multiplexer #(.width(3), .enable("false")) multiplexer_2 (
    .in0(priority_encoder_2_out), .in1(3'b100), .out(multiplexer_2_out), .sel(latch_double_fault));
  Comparator #(.width(3), .mode("unsigned")) comparator_1 (
    .a(exc_internal_vec), .b(3'b111), .eq(comparator_1_eq));  // open: gt, lt
  assign bit_extender_1_out = {{13{1'b0}}, exc_internal_vec};  // Bit_Extender bit_extender_1
  assign bit_extender_2_out = {{10{1'b0}}, exc_vec_t};  // Bit_Extender bit_extender_2
  assign bit_extender_3_out = {{10{1'b0}}, exc_vec};  // Bit_Extender bit_extender_3
  assign bit_extender_4_out = {{13{1'b0}}, 3'b100};  // Bit_Extender bit_extender_4
  Register #(.width(16), .trigger("falling")) register_6 (.D(busD), .en(and_13_out), .Q(R4), .clk(clk));  // open: clr
  Register #(.width(16), .trigger("falling")) register_7 (.D(busD), .en(and_17_out), .Q(R5), .clk(clk));  // open: clr
  and and_17 (and_17_out, decoder_1_out5, r_latch);
  and and_18 (and_18_out, r_asrtD, decoder_1_out5);
  assign busD = and_15_out ? R4 : 16'bz;  // Controlled_Buffer controlled_buffer_5
  Register #(.width(3), .trigger("falling")) register_8 (
    .D(multiplexer_2_out), .en(priority_encoder_2_gs), .Q(exc_internal_vec), .clk(clk_no_inhibit));  // open: clr
  Multiplexer #(.width(16), .enable("false")) multiplexer_3 (
    .in0(bit_extender_1_out), .in1(bit_extender_2_out), .out(multiplexer_3_out), .sel(comparator_1_eq));
  Multiplexer #(.width(16), .enable("false")) multiplexer_4 (
    .in0(bit_extender_3_out), .in1(bit_extender_4_out), .out(multiplexer_4_out), .sel(latch_double_fault));
  and and_19 (IAck, fetch, and_20_out);
  and and_20 (and_20_out, IRQ, PS[15]);
  or or_7 (latch_int, and_20_out, exc_triggered);
  and and_21 (reset_exc, exc_triggered, fetch);
  Register #(.width(16), .trigger("falling")) register_9 (.D(busD), .en(and_22_out), .Q(R6), .clk(clk));  // open: clr
  and and_22 (and_22_out, decoder_1_out6, r_latch);
  and and_23 (and_23_out, r_asrtD, decoder_1_out6);
  assign busD = and_23_out ? R6 : 16'bz;  // Controlled_Buffer controlled_buffer_6
  assign busD = and_18_out ? R5 : 16'bz;  // Controlled_Buffer controlled_buffer_7
  S_R_Flip_Flop #(.trigger("falling")) s_r_ff_4 (
    .S(priority_encoder_2_gs), .clk(clk_no_inhibit), .R(reset_exc), .Q(exc_latch));  // open: Qn, preset, reset, en
  assign bit_extender_5_out = {{10{1'b0}}, int_vec};  // Bit_Extender bit_extender_5
  Multiplexer #(.width(16), .enable("false")) multiplexer_5 (
    .in0(multiplexer_3_out), .in1(multiplexer_4_out), .out(multiplexer_5_out), .sel(EXC));
  Register #(.width(16), .trigger("falling")) register_10 (.D(busD), .en(and_24_out), .Q(FP), .clk(clk));  // open: clr
  and and_24 (and_24_out, decoder_1_out7, r_latch);
  and and_25 (and_25_out, r_asrtD, decoder_1_out7);
  assign busD = and_25_out ? FP : 16'bz;  // Controlled_Buffer controlled_buffer_8
  and and_26 (critical_fault, double_fault, priority_encoder_2_gs);
  or or_8 (exc_triggered, priority_encoder_2_gs, exc_latch);
  Multiplexer #(.width(16), .enable("false")) multiplexer_6 (
    .in0(bit_extender_5_out), .in1(multiplexer_5_out), .out(multiplexer_6_out), .sel(exc_triggered));
  assign or_9_out = multiplexer_6_out | 16'h8000;  // OR_Gate or_9, 16 bits wide
  Multiplexer #(.select(3), .width(16)) multiplexer_7 (
    .in0(R0), .in1(R1), .in2(R2), .in3(R3), .in4(R4), .in5(R5), .in6(R6), .in7(FP), .out(bus0), .sel(rs0),
    .en(r_asrt0));
  Multiplexer #(.select(3), .width(16)) multiplexer_8 (
    .in0(R0), .in1(R1), .in2(R2), .in3(R3), .in4(R4), .in5(R5), .in6(R6), .in7(FP), .out(bus1), .sel(rs1),
    .en(r_asrt1));
  Multiplexer #(.width(16), .enable("false")) multiplexer_9 (
    .in0(busD), .in1(or_9_out), .out(multiplexer_9_out), .sel(latch_int));
  Multiplexer #(.width(16), .enable("false")) multiplexer_10 (
    .in0(multiplexer_9_out), .in1(16'h8200), .out(fetched_instruction), .sel(startup));
  not not_4 (not_4_out, fetch);
  or or_10 (or_10_out, latch_int, startup);
  Register #(.width(16), .trigger("falling")) register_11 (
    .D(fetched_instruction), .en(fetch),
    .Q({register_11_q, br_rel_flags_d[3], alu_op_d1, alu_op_d0, imm6_d, br_abs_flags_d}), .clk(clk),
    .clr(and_27_out));
  and and_27 (and_27_out, fetch, not_4_out);
  D_Flip_Flop #(.trigger("falling")) d_ff_4 (
    .clk(clk), .D(or_10_out), .Q(virtual_instruction), .en(fetch));  // open: Qn, preset, reset
  Multiplexer #(.enable("false")) multiplexer_11 (
    .in0(br_rel_nop), .in1(virtual_instruction), .out(pc_inc_inhibit), .sel(exc_triggered));
  assign bus0 = fp_asrt0 ? FP : 16'bz;  // Controlled_Buffer controlled_buffer_9
  assign bus1 = imm_asrt1 ? imm : 16'bz;  // Controlled_Buffer controlled_buffer_10
  assign busD = imm_asrtD ? imm : 16'bz;  // Controlled_Buffer controlled_buffer_11
  Decoder #(.select(3), .disabled(0), .enable("false")) decoder_2 (
    .out0(decoder_2_out0), .out1(_1op), .out2(decoder_2_out2), .out3(imm6), .out4(imm9),
    .out5(decoder_2_out5), .out6(decoder_2_out6), .out7(decoder_2_out7), .sel(register_11_q));
  Comparator #(.width(16), .mode("unsigned")) comparator_2 (
    .a(16'h8004), .b({register_11_q, br_rel_flags_d[3], alu_op_d1, alu_op_d0, imm6_d, br_abs_flags_d}),
    .eq(double_fault));  // open: gt, lt
  // Probe on sp_register_1_mon
  sp_register sp_register_1 (
    .In(busD), .plus_2(sp_inc), .en(sp_latch), .minus_2(sp_dec), .clk(clk), .Mon(sp_register_1_mon), .Out(SP));  // open: clr
  Demultiplexer #(.disabled(0), .enable("false")) demultiplexer_1 (
    .out0(demultiplexer_1_out0), .out1(shifts), .in(decoder_2_out0), .sel(br_rel_flags_d[3]));
  Demultiplexer #(.select(2), .disabled(0), .enable("false")) demultiplexer_2 (
    .out0(_2op), .out1(alu3_ind), .out2(mem2), .out3(alu2), .in(decoder_2_out2),
    .sel({br_rel_flags_d[3], alu_op_d1[2]}));
  Demultiplexer #(.disabled(0), .enable("false")) demultiplexer_3 (
    .out0(mem3), .out1(alu3), .in(decoder_2_out5), .sel(br_rel_flags_d[3]));
  assign bus0 = sp_asrt0 ? SP : 16'bz;  // Controlled_Buffer controlled_buffer_12
  Demultiplexer #(.disabled(0), .enable("false")) demultiplexer_4 (
    .out0(_0op), .out1(br_abs_d), .in(demultiplexer_1_out0), .sel(alu_op_d1[2]));
  Multiplexer #(.width(4), .enable("false")) multiplexer_12 (
    .in0({br_rel_flags_d[3], alu_op_d1}), .in1(br_abs_flags_d), .out(multiplexer_12_out), .sel(br_abs_d));
  branch_logic branch_logic_1 (.cccc(multiplexer_12_out), .CVZN(ps_flags), .go(branch_logic_1_go));
  assign busD = x_mdu_asrtD ? mdu_out : 16'bz;  // Controlled_Buffer controlled_buffer_13
  assign bus0 = pc_asrt0 ? PC : 16'bz;  // Controlled_Buffer controlled_buffer_14
  // Probe on pc_register_1_mon
  and and_28 (and_28_out, pc_inc, not_8_out);
  pc_register pc_register_1 (
    .In(busD), .en(pc_latch), .plus_2(and_28_out), .Out(PC), .clk(clk), .Mon(pc_register_1_mon),
    .asrt_inc(and_29_out), .inverse_inc(exc_triggered));  // open: clr
  and and_29 (and_29_out, jsr, pc_asrtD);
  and and_30 (br_abs_nop, br_abs_d, not_5_out);
  not not_5 (not_5_out, br_abs);
  and and_31 (br_abs, br_abs_d, branch_logic_1_go);
  and and_32 (and_32_out, decoder_2_out6, not_6_out);
  not not_6 (not_6_out, br_rel_n);
  and and_33 (br_rel_n, decoder_2_out6, branch_logic_1_go);
  and and_34 (and_34_out, decoder_2_out7, not_7_out);
  not not_7 (not_7_out, br_rel_p);
  and and_35 (br_rel_p, decoder_2_out7, branch_logic_1_go);
  not not_8 (not_8_out, pc_inc_inhibit);
  assign busD = sp_asrtD ? SP : 16'bz;  // Controlled_Buffer controlled_buffer_15
  Multiplexer #(.enable("false")) multiplexer_13 (
    .in0(and_36_out), .in1(PS[3]), .out(multiplexer_13_out), .sel(arith_carry));
  alu alu_1 (
    .A(bus0), .B(bus1), .Cin(multiplexer_13_out), .func(alu_func), .op_type(alu_op_type), .C(cout),
    .V(CVZN[2]), .Z(CVZN[1]), .N(CVZN[0]), .S(address), .shift_count(alu_op_d0));
  assign busD = pc_asrtD ? PC : 16'bz;  // Controlled_Buffer controlled_buffer_16
  or or_11 (or_11_out, alu_op_d1[1], alu_op_d1[2], br_rel_flags_d[3]);
  not not_9 (not_9_out, br_abs_flags_d[3]);
  or or_12 (br_rel_nop, and_32_out, and_34_out);
  mdu mdu_1 (
    ._1st_argument(bus0), ._2nd_argument(bus1), .en(x_mdu_asrtD), .optype(alu_op_d0[1:0]), .out_9(mdu_out),
    .clk(clk), .phase(x_mdu_phase), .phase_part(x_mdu_phase_part), .mdu_exception(mdu_exc));
  and and_36 (and_36_out, mem, inc_address);
  assign busD = alu_asrtD ? address : 16'bz;  // Controlled_Buffer controlled_buffer_17
  and and_37 (\int , imm9, not_10_out);
  not not_10 (not_10_out, or_11_out);
  Decoder #(.select(2), .disabled(0)) decoder_3 (
    .out0(halt), .out1(\wait ), .out2(ei), .out3(di), .sel(br_abs_flags_d[1:0]), .en(and_38_out));
  and and_38 (and_38_out, and_39_out, not_11_out);
  and and_39 (and_39_out, br_abs_flags_d[2], not_9_out, _0op);
  not not_11 (not_11_out, exc_triggered);
  or or_13 (or_13_out, shifts, alu2);
  assign bit_extender_6_out = {{7{1'b0}}, {alu_op_d0, imm6_d, br_abs_flags_d}};  // Bit_Extender bit_extender_6
  assign bit_extender_7_out = {{7{1'b1}}, {alu_op_d0, imm6_d, br_abs_flags_d}};  // Bit_Extender bit_extender_7
  Multiplexer #(.select(2), .width(16), .disabled(0), .enable("false")) multiplexer_14 (
    .in0(bit_extender_6_out), .in1(bit_extender_7_out), .in2(bit_extender_8_out), .in3(bit_extender_9_out),
    .out(multiplexer_14_out), .sel({imm6, imm_extend_negative}));
  assign bit_extender_8_out = {{10{1'b0}}, {alu_op_d0, imm6_d, br_abs_flags_d[3]}};  // Bit_Extender bit_extender_8
  assign bit_extender_9_out = {{10{1'b1}}, {alu_op_d0, imm6_d, br_abs_flags_d[3]}};  // Bit_Extender bit_extender_9
  LED led_1 (.in(clk));
  LED led_2 (.in(PS[15]));
  // Probe on ps_flags
  ps_register ps_register_1 (
    .flags({cout, CVZN}), .word(busD), .clk(clk), .out(PS), .out_flags(ps_flags),
    .latch_flags(ps_latch_flags), .latch_word(ps_latch_word), .ei(ei), .di(di));
  or or_14 (or_14_out, br_abs_nop, br_rel_nop);
  LED led_3 (.in(clk_no_inhibit));
  assign busD = ps_asrtD ? PS : 16'bz;  // Controlled_Buffer controlled_buffer_18
  or or_15 (or_15_out, br_abs_flags_d[1], br_abs_flags_d[2]);
  not not_12 (not_12_out, or_15_out);
  Priority_Encoder priority_encoder_3 (
    .in0(_0op), .in1(_1op), .in2(_2op), .in3(mem2), .in4(imm6), .in5(imm9), .in6(mem3),
    .in7(priority_encoder_4_gs), .out(priority_encoder_3_out));  // open: en_in, gs, en_out
  Priority_Encoder priority_encoder_4 (
    .in0(br_abs), .in1(or_13_out), .in2(alu3_ind), .in3(alu3), .in4(br_rel_p), .in5(br_rel_n),
    .in6(or_14_out), .in7(fetch), .out(priority_encoder_4_out), .gs(priority_encoder_4_gs));  // open: en_in, en_out
  or or_16 (or_16_out[0], alu3, alu3_ind);
  Decoder #(.disabled(0)) decoder_4 (.out0(jsr), .out1(rti), .sel(br_abs_flags_d[0]), .en(and_40_out));
  and and_40 (and_40_out, not_12_out, br_abs_flags_d[3], _0op);
  Multiplexer #(.select(3), .width(4), .disabled(0), .enable("false")) multiplexer_15 (
    .in0(br_abs_flags_d), .in1({alu_op_d0[0], imm6_d, br_abs_flags_d[3]}), .in2({alu_op_d1[0], alu_op_d0}),
    .in3({alu_op_d1[0], alu_op_d0}), .in4({br_rel_flags_d[3], alu_op_d1}),
    .in5({br_rel_flags_d[3], alu_op_d1}), .in6({br_rel_flags_d[3], alu_op_d1}), .in7(bit_extender_10_out),
    .out(multiplexer_15_out), .sel(priority_encoder_3_out));
  assign bit_extender_10_out = {{1{1'b0}}, priority_encoder_4_out};  // Bit_Extender bit_extender_10
  or or_17 (or_17_out, shifts, alu2, or_16_out[0]);
  Shifter #(.width(16)) shifter_1 (.in(multiplexer_14_out), .\dist (4'b0001), .out(shifter_1_out));
  Shifter #(.width(16)) shifter_2 (.in(multiplexer_14_out), .\dist (4'b0010), .out(shifter_2_out));
  Multiplexer #(.width(3), .enable("false")) multiplexer_16 (
    .in0(3'b001), .in1({shifts, alu2, or_16_out[0]}), .out(alu_op_type), .sel(or_17_out));
  Multiplexer #(.width(16), .disabled(0), .enable("false")) multiplexer_17 (
    .in0(multiplexer_14_out), .in1(shifter_1_out), .out(multiplexer_17_out), .sel(imm_shift));
  Multiplexer #(.width(16), .disabled(0), .enable("false")) multiplexer_18 (
    .in0(shifter_2_out), .in1(or_18_out), .out(multiplexer_18_out), .sel(phase[0]));
  assign or_18_out = shifter_2_out | 16'h2;  // OR_Gate or_18, 16 bits wide
  or or_19 (or_19_out, io_phase, clk_inhibit);
  not not_13 (not_13_out, or_19_out);
  assign busD = rd_wr_prime ? bus_control_1_to_bus : 16'bz;  // Controlled_Buffer controlled_buffer_19
  Multiplexer #(.width(16), .disabled(0), .enable("false")) multiplexer_19 (
    .in0(multiplexer_17_out), .in1(multiplexer_18_out), .out(imm), .sel(\int ));
  and and_41 (word, word_t, not_13_out);
  bus_control bus_control_1 (
    .sign_extend(sign_extend), .odd_address(address[0]), .word(word_t), .clk_no_inhibit(clk_no_inhibit),
    .from_bus(busD), .data_in(data_in), .inc_address(inc_address), .clk_inhibit(clk_inhibit),
    .data_out(data_out), .to_bus(bus_control_1_to_bus), .phase(io_phase));
  Comparator #(.width(30)) comparator_3 (.a({30{1'b0}}), .b(rom_1_data), .eq(comparator_3_eq));  // open: gt, lt
  and and_42 (exc_trig_sp, rom_1_data[25], busD[0]);
  and and_43 (exc_trig_pc, busD[0], rom_1_data[11]);
  ROM #(.addrWidth(10), .dataWidth(30)) rom_1 (
    .addr({phase, priority_encoder_3_out, multiplexer_15_out}), .data(rom_1_data));  // open: sel
  ROM #(.addrWidth(10), .dataWidth(30)) rom_2 (
    .addr({phase, priority_encoder_3_out, multiplexer_15_out}), .data(rom_2_data));  // open: sel
  or or_20 (or_20_out, _1op, _2op, alu3_ind);
  Multiplexer #(.width(3), .disabled(0), .enable("false")) multiplexer_20 (
    .in0(alu_op_d0), .in1(br_abs_flags_d[2:0]), .out(rs1), .sel(or_20_out));
  Multiplexer #(.width(3), .disabled(0), .enable("false")) multiplexer_21 (
    .in0({imm6_d, br_abs_flags_d[3]}), .in1(br_abs_flags_d[2:0]), .out(rs0), .sel(imm6));
  and and_44 (exc_trig_invalid_inst, comparator_3_eq, not_14_out);
  not not_14 (not_14_out, exc_latch);
  Multiplexer #(.width(30), .enable("false")) multiplexer_22 (
    .in0(rom_1_data), .in1(rom_2_data), .out(multiplexer_22_out), .sel(exc_triggered));
  and and_45 (and_45_out, alu_op_d1[1], alu_op_d1[2], br_rel_flags_d[3]);
  Multiplexer #(.width(30), .enable("false")) multiplexer_23 (
    .in0(multiplexer_22_out), .in1(30'h20000000),
    .out({CUT, x_mdu_sigswap, x_mdu_asrtD, word_t, sp_latch, sp_inc, sp_dec, sp_asrtD, sp_asrt0, sign_extend, rd_wr_prime, r_latch, r_asrtD, r_asrt1, r_asrt0, ps_latch_word, ps_latch_flags, ps_asrtD, pc_latch, pc_inc, pc_asrtD, pc_asrt0, mem, imm_shift, imm_extend_negative, imm_asrtD, imm_asrt1, fp_asrt0, data_ins_prime, alu_asrtD}),
    .sel(or_21_out));
  or or_21 (or_21_out, status[1], startup, and_46_out);
  and and_46 (and_46_out, latch_int, fetch);
  and and_47 (and_47_out, imm6, and_45_out);
  or or_22 (arith_carry, shifts, alu3);
  or or_23 (or_23_out, alu2, alu3_ind);
  Multiplexer #(.width(3), .enable("false")) multiplexer_24 (
    .in0(3'b101), .in1(3'b110), .out(multiplexer_24_out), .sel(and_47_out));
  Multiplexer #(.width(3), .enable("false")) multiplexer_25 (
    .in0(alu_op_d1), .in1(alu_op_d0), .out(multiplexer_25_out), .sel(or_23_out));
  or or_24 (or_24_out, or_23_out, arith_carry);
  Multiplexer #(.width(3), .enable("false")) multiplexer_26 (
    .in0(multiplexer_24_out), .in1(multiplexer_25_out), .out(alu_func), .sel(or_24_out));

  // Other names for the same wires on the sheet: data = data_ins_prime; read = rd_wr_prime;
  //   address_out[15:0] = address; busA[15:0] = address; CVZN[3] = cout; direct_exc_vec[5:0] = exc_vec;
  //   exc_trig_ext = EXC; imm9_d[8:0] = {alu_op_d0, imm6_d, br_abs_flags_d}; op_type_d0[3:0] = br_abs_flags_d;
  //   rd[2:0] = br_abs_flags_d[2:0]; rd_d[2:0] = br_abs_flags_d[2:0];
  //   imm6_d (some bits) = {alu_op_d0, br_abs_flags_d[3]};
  //   op_type_d1[3:0] = {alu_op_d0[0], imm6_d, br_abs_flags_d[3]}; rs0_d[2:0] = {imm6_d, br_abs_flags_d[3]};
  //   op_type_d2[3:0] = {alu_op_d1[0], alu_op_d0}; op_type_mdu[1:0] = alu_op_d0[1:0]; rs1_d[2:0] = alu_op_d0;
  //   shift_count_d[2:0] = alu_op_d0; br_rel_flags_d[2:0] = alu_op_d1;
  //   op_type_d3[3:0] = {br_rel_flags_d[3], alu_op_d1}; XY[1:0] = {br_rel_flags_d[3], alu_op_d1[2]}; Y = alu_op_d1[2];
  //   X = br_rel_flags_d[3]; pc_value[15:0] = PC; ps_value[15:0] = PS; cin = PS[3]; int_en = PS[15];
  //   sp_value[15:0] = SP

  // Notes on the sheet:
  //   EXC: pull=down
  //   hold: pull=down
  //   IRQ: pull=down
  //   clock: pull=down
  //   data_in: pull=down
  //   0 - running
  //   1 - waiting
  //   2 - halted
  //   3 - fault
  //   2
  //   3
  //   1
  //   int, reset, rti
  //   Double fault: 1. Unrecoverable instruction
  //   2. Multiple exceptions on the same phase
  //   3. Mutiple exceptions across several phases
  //   SP
  //   Coco-de-Mer 16
  //   Designed by Nikolay Repin
  //   2023
  //   PС
  //   int, reset
  //   CVZN
  //   PS
  //   1, 3, 5, 7
  //   contents of rom_1 (hex, n*v repeats v):
  //   4*0 4*24000000 4a00282 5280882 24a00282 25280882 24e00082 26280082 24a01082 25284082 24a20082
  //   252c0082 240c0580 4a00282 20440000 22020000 20041000 20024000 20040200 20020800 22210001 5*0
  //   2004a001 11*0 4*8018000 240c8082 200c8082 201c8082 240c8080 200c8080 201c8080 24028082 20028082 8*0
  //   240c00ce 240c00ee 200c008e 200c00ae 201c008e 201c00ae 240200ce 240200ee 2002008e 200200ae 20040010
  //   20040030 2004a009 2004a029 2000a008 2000a028 4a01082 4080888 24a00092 24a000b2 22200049 22200069
  //   4a00282 4a00282 8*0 240d8082 200d8082 201d8082 240d8080 200d8080 201d8080 24038082 20038082 8*0
  //   24080980 2004a001 2001a000 2005a001 20000949 20000969 20000400 24080580 16*0 24080980 25284082 9*0
  //   20020800 24*0 4*8040000 32*0 4a00282 24084088 4*0 20000949 20000969 84*0 4*38040000 32*0 4080888
  //   127*0 24084088
  //   contents of rom_2 (hex, n*v repeats v):
  //   4*0 4*24000000 4a00282 5280082 4a00282 5280082 4e00082 4280082 4a01082 5280082 4a20082 5280082
  //   24080580 4a00282 400000 20000 1000 20000 200 20000 210001 5*0 8001 11*0 4*8018000 24088482 20088482
  //   20188482 24088480 20088480 20188480 24028482 20028482 8*0 240804ce 240804ee 2008048e 200804ae
  //   2018048e 201804ae 240204ce 240204ee 2002048e 200204ae 20000410 20000430 2000a409 2000a429 20008408
  //   20008428 4a01082 4080088 4a00092 4a000b2 20200449 20200469 4a00282 4a00282 8*0 24098482 20098482
  //   20198482 24098480 20098480 20198480 24038482 20038482 8*0 24080580 20008401 20018400 20018401
  //   20000549 20000569 20000400 24080180 16*0 4080180 5280082 21000400 20800400 21000400 20000400
  //   21000400 20800400 21000400 20800400 0 20000 7*20000400 5*0 20000400 11*0 4*8000000 32*0 4a00282
  //   4080088 21000400 21000400 0 0 149 169 48*0 21000400 800000 9*0 21000400 24*0 4*38000000 32*0 4080088
  //   20000400 4*0 21000400 21000400 49*0 20800400 70*0 4080088 127*0 1000000 127*0 21000400
endmodule

module mdu (
  input  en,
  input  [1:0] optype,
  input  clk,
  input  [15:0] _1st_argument,
  input  [15:0] _2nd_argument,
  output mdu_exception,
  output phase,
  output phase_part,
  output [15:0] out_9
);

  wire isBzero, isNegA, isNegB, isNegOutput, isPhase0, isSign, not_1_out, not_3_out, or_1_out, sdiv, smul,
       udiv, umul;
  wire [15:0] A, Areg, B, Breg, data_A, data_B, demultiplexer_1_out0, demultiplexer_1_out1,
       demultiplexer_2_out0, demultiplexer_2_out1, demultiplexer_3_out1, demultiplexer_6_out1, divider_1_out,
       divider_1_rem, multiplexer_3_out, multiplexer_4_out, multiplexer_5_out, multiplier_1_cout,
       multiplier_1_out, sdiv_q_between, sdiv_q_out, sdiv_q_out_neg, sdiv_rem_out, sdiv_res,
       sign_load_1_out_2, sign_load_2_out_2, smul_c_out, smul_c_out0, smul_c_out1, smul_out, smul_res,
       udiv_q_out, udiv_rem_out, udiv_res, umul_c_out, umul_out, umul_res;
  wire [31:0] controlled_buffer_4_out, smul_32bit_number, smul_32bitnum_out_neg;

  Controlled_Buffer controlled_buffer_1 (.en(en));  // open: in, out
  Decoder #(.select(2), .disabled(0)) decoder_1 (
    .out0(umul), .out1(smul), .out2(udiv), .out3(sdiv), .sel(optype), .en(en));
  and and_1 (mdu_exception, en, isPhase0, not_1_out, isBzero);
  not not_1 (not_1_out, optype[1]);
  zero16 zero16_1 (.in(Breg), .zero(isBzero));
  assign data_A = isPhase0 ? _1st_argument : 16'bz;  // Controlled_Buffer controlled_buffer_2
  assign data_B = isPhase0 ? _2nd_argument : 16'bz;  // Controlled_Buffer controlled_buffer_3
  xor xor_1 (isNegOutput, isNegA, isNegB);
  not not_2 (isPhase0, or_1_out);
  or or_1 (or_1_out, phase, phase_part);
  Demultiplexer #(.width(16), .disabled(0), .enable("false")) demultiplexer_1 (
    .out0(demultiplexer_1_out0), .out1(demultiplexer_1_out1), .in(Areg), .sel(isSign));
  or or_2 (isSign, sdiv, smul);
  Demultiplexer #(.width(16), .disabled(0), .enable("false")) demultiplexer_2 (
    .out0(demultiplexer_2_out0), .out1(demultiplexer_2_out1), .in(Breg), .sel(isSign));
  Counter #(.width(2), .max('h3)) counter_1 (
    .count(en), .Q({phase, phase_part}), .clk(clk), .clr(not_3_out));  // open: load, D, carry
  not not_3 (not_3_out, en);
  sign_load sign_load_1 (.in_1(demultiplexer_1_out1), .out_2(sign_load_1_out_2), .out_3(isNegA));
  sign_load sign_load_2 (.in_1(demultiplexer_2_out1), .out_2(sign_load_2_out_2), .out_3(isNegB));
  Register #(.width(16)) register_1 (.D(data_A), .en(isPhase0), .Q(Areg), .clk(clk));  // open: clr
  Register #(.width(16)) register_2 (.D(data_B), .en(isPhase0), .Q(Breg), .clk(clk));  // open: clr
  Multiplexer #(.width(16), .enable("false")) multiplexer_1 (
    .in0(demultiplexer_1_out0), .in1(sign_load_1_out_2), .out(A), .sel(isSign));
  Multiplexer #(.width(16), .enable("false")) multiplexer_2 (
    .in0(demultiplexer_2_out0), .in1(sign_load_2_out_2), .out(B), .sel(isSign));
  Demultiplexer #(.width(16), .disabled(0), .enable("false")) demultiplexer_3 (
    .out0(smul_c_out0), .out1(demultiplexer_3_out1), .in(smul_32bit_number[31:16]), .sel(isNegOutput));
  Demultiplexer #(.width(16), .disabled(0), .enable("false")) demultiplexer_4 (
    .out0(umul_c_out), .out1(smul_32bit_number[31:16]), .in(multiplier_1_cout), .sel(isSign));
  Multiplexer #(.width(16), .enable("false")) multiplexer_3 (
    .in0(smul_c_out), .in1(smul_32bitnum_out_neg[31:16]), .out(multiplexer_3_out), .sel(isNegOutput));
  Multiplexer #(.width(16), .enable("false")) multiplexer_4 (
    .in0(smul_out), .in1(smul_32bitnum_out_neg[15:0]), .out(multiplexer_4_out), .sel(isNegOutput));
  Multiplexer #(.width(16), .enable("false")) multiplexer_5 (
    .in0(sdiv_q_out), .in1(sdiv_q_out_neg), .out(multiplexer_5_out), .sel(isNegOutput));
  Negator #(.width(16)) negator_1 (.in(demultiplexer_3_out1), .out(smul_c_out1));
  assign controlled_buffer_4_out = isNegOutput ? smul_32bit_number : 32'bz;  // Controlled_Buffer controlled_buffer_4
  Demultiplexer #(.width(16), .disabled(0), .enable("false")) demultiplexer_5 (
    .out0(umul_out), .out1(smul_32bit_number[15:0]), .in(multiplier_1_out), .sel(isSign));
  Multiplier #(.width(16)) multiplier_1 (.a(A), .b(B), .out(multiplier_1_out), .cout(multiplier_1_cout));  // open: cin
  Multiplexer #(.width(16)) multiplexer_6 (.in0(umul_c_out), .in1(umul_out), .out(umul_res), .sel(phase_part), .en(en));
  Multiplexer #(.width(16)) multiplexer_7 (
    .in0(multiplexer_3_out), .in1(multiplexer_4_out), .out(smul_res), .sel(phase_part), .en(en));
  Multiplexer #(.width(16)) multiplexer_8 (
    .in0(udiv_rem_out), .in1(udiv_q_out), .out(udiv_res), .sel(phase_part), .en(en));
  Multiplexer #(.width(16)) multiplexer_9 (
    .in0(sdiv_rem_out), .in1(multiplexer_5_out), .out(sdiv_res), .sel(phase_part), .en(en));
  Negator #(.width(32)) negator_2 (.in(controlled_buffer_4_out), .out(smul_32bitnum_out_neg));
  Demultiplexer #(.width(16), .disabled(0), .enable("false")) demultiplexer_6 (
    .out0(sdiv_q_out), .out1(demultiplexer_6_out1), .in(sdiv_q_between), .sel(isNegOutput));
  Divider #(.width(16)) divider_1 (.a(A), .b(B), .out(divider_1_out), .rem(divider_1_rem));  // open: upper
  Demultiplexer #(.width(16), .disabled(0), .enable("false")) demultiplexer_7 (
    .out0(udiv_rem_out), .out1(sdiv_rem_out), .in(divider_1_rem), .sel(isSign));
  Demultiplexer #(.width(16), .disabled(0), .enable("false")) demultiplexer_8 (
    .out0(udiv_q_out), .out1(sdiv_q_between), .in(divider_1_out), .sel(isSign));
  Multiplexer #(.select(2), .width(16), .disabled(0)) multiplexer_10 (
    .in0(umul_res), .in1(smul_res), .in2(udiv_res), .in3(sdiv_res), .out(out_9), .sel(optype), .en(en));
  Negator #(.width(16)) negator_3 (.in(demultiplexer_6_out1), .out(sdiv_q_out_neg));

  // Other names for the same wires on the sheet: mdu_exc = mdu_exception;
  //   smul_between[15:0] = smul_32bit_number[15:0]; smul_c_between[15:0] = smul_32bit_number[31:16];
  //   smul_out_neg[15:0] = smul_32bitnum_out_neg[15:0]; smul_c_out_neg[15:0] = smul_32bitnum_out_neg[31:16]

  // Notes on the sheet:
  //   2.
  //   It might be extended by logical or 
  //   improve performance by logic or then not
  //   1.
  //   Improve this:
  //   quotient is negative, not remainder
  //   1.Phase_part because mdu's value latches only with r_latch in second half
  //   2. Loading data(arguments) only when function from extension was called
endmodule

module sp_register (
  input  [15:0] In,
  input  clr,
  input  clk,
  input  plus_2,
  input  en,
  input  minus_2,
  output [15:0] Out,
  output [15:0] Mon
);

  wire count, en_t;
  wire [15:0] incdec2_1_out, multiplexer_1_out;

  Register #(.width(16), .trigger("falling")) register_1 (
    .D(multiplexer_1_out), .en(en_t), .Q(Mon), .clk(clk), .clr(clr));
  Multiplexer #(.width(16), .disabled(0), .enable("false")) multiplexer_1 (
    .in0(In), .in1(incdec2_1_out), .out(multiplexer_1_out), .sel(count));
  or or_1 (count, plus_2, minus_2);
  or or_2 (en_t, count, en);
  incdec2 incdec2_1 (.in(Mon), .out(incdec2_1_out), .inc_dec_prime(plus_2));
  Multiplexer #(.width(16), .disabled(0), .enable("false")) multiplexer_2 (
    .in0(Mon), .in1(incdec2_1_out), .out(Out), .sel(minus_2));

  // Notes on the sheet:
  //   en: pull=up
  //   clk: pull=down
  //   clr: pull=down
  //   plus_2: pull=down
  //   minus_2: pull=down
endmodule

module pc_register (
  input  [15:0] In,
  input  clr,
  input  clk,
  input  en,
  input  plus_2,
  input  asrt_inc,
  input  inverse_inc,
  output [15:0] Out,
  output [15:0] Mon
);

  wire en_t, not_1_out;
  wire [15:0] incdec2_1_out, multiplexer_1_out;

  Multiplexer #(.width(16), .disabled(0), .enable("false")) multiplexer_1 (
    .in0(In), .in1(incdec2_1_out), .out(multiplexer_1_out), .sel(plus_2));
  Register #(.width(16), .trigger("falling")) register_1 (
    .D(multiplexer_1_out), .en(en_t), .Q(Mon), .clk(clk), .clr(clr));
  or or_1 (en_t, plus_2, en);
  incdec2 incdec2_1 (.in(Mon), .out(incdec2_1_out), .inc_dec_prime(not_1_out));
  not not_1 (not_1_out, inverse_inc);
  Multiplexer #(.width(16), .disabled(0), .enable("false")) multiplexer_2 (
    .in0(Mon), .in1(incdec2_1_out), .out(Out), .sel(asrt_inc));

  // Other names for the same wires on the sheet: count = plus_2

  // Notes on the sheet:
  //   plus_2: pull=down
  //   clr: pull=down
  //   clk: pull=down
  //   en: pull=up
  //   asrt_inc: pull=down
  //   inverse_inc: pull=down
endmodule

module ps_register (
  input  [3:0] flags,
  input  [15:0] word,
  input  clk,
  input  latch_word,
  input  latch_flags,
  input  ei,
  input  di,
  output [3:0] out_flags,
  output [15:0] out
);

  wire or_1_out, or_3_out, set_int_flag;
  wire [15:0] multiplexer_1_out, multiplexer_2_out;

  Multiplexer #(.width(16), .enable("false")) multiplexer_1 (
    .in0({out[15:4], flags}), .in1({ei, out[14:0]}), .out(multiplexer_1_out), .sel(set_int_flag));
  Multiplexer #(.width(16), .enable("false")) multiplexer_2 (
    .in0(multiplexer_1_out), .in1(word), .out(multiplexer_2_out), .sel(latch_word));
  or or_1 (or_1_out, latch_word, latch_flags);
  or or_2 (set_int_flag, ei, di);
  Register #(.width(16), .trigger("falling")) register_1 (
    .D(multiplexer_2_out), .en(or_3_out), .Q(out), .clk(clk));  // open: clr
  or or_3 (or_3_out, or_1_out, set_int_flag);
  Bit_Extender #(.in_width(16), .out_width(4)) bit_extender_1 (.in(out), .out(out_flags));

  // Notes on the sheet:
  //   di: pull=down
  //   latch_word: pull=down
  //   clk: pull=down
  //   word: pull=down
  //   latch_flags: pull=down
  //   ei: pull=down
  //   flags: pull=down
endmodule

module incdec2 (
  input  [15:0] in,
  input  inc_dec_prime,
  output [15:0] out
);

  wire [15:0] multiplexer_1_out;

  Multiplexer #(.width(16), .enable("false")) multiplexer_1 (
    .in0(16'hfffe), .in1(16'h2), .out(multiplexer_1_out), .sel(inc_dec_prime));
  Adder #(.width(16)) adder_1 (.a(in), .b(multiplexer_1_out), .out(out));  // open: cin, cout

  // Notes on the sheet:
  //   inc_dec_prime: pull=up
endmodule

module bus_control (
  input  sign_extend,
  input  odd_address,
  input  word,
  input  clk_no_inhibit,
  input  [15:0] from_bus,
  input  [15:0] data_in,
  output inc_address,
  output clk_inhibit,
  output phase,
  output [15:0] data_out,
  output [15:0] to_bus
);

  wire and_1_out;
  wire [7:0] bit_extender_1_out, register_1_q;
  wire [15:0] bytes_swap_1_out, make_byte_2_out, multiplexer_1_out, multiplexer_3_out, multiplexer_5_out,
       n2s_compliment_1_out;

  Bit_Extender #(.in_width(16), .out_width(8)) bit_extender_1 (.in(data_in), .out(bit_extender_1_out));
  and and_1 (and_1_out, clk_inhibit, clk_no_inhibit);
  Register #(.trigger("falling")) register_1 (
    .D(bit_extender_1_out), .Q(register_1_q), .clk(and_1_out));  // open: en, clr
  and and_2 (clk_inhibit, odd_address, word);
  make_byte make_byte_1 ();  // open: In, Out
  Multiplexer #(.width(16), .disabled(0), .enable("false")) multiplexer_1 (
    .in0(from_bus), .in1(bytes_swap_1_out), .out(multiplexer_1_out), .sel(inc_address));
  bytes_swap bytes_swap_1 (.In(from_bus), .Out(bytes_swap_1_out));
  make_byte make_byte_2 (.In(data_in), .Out(make_byte_2_out));
  _2s_compliment u_2s_compliment_1 (.In(data_in), .Out(n2s_compliment_1_out));
  D_Flip_Flop #(.trigger("falling")) d_ff_1 (
    .clk(clk_no_inhibit), .D(clk_inhibit), .Q(inc_address));  // open: Qn, preset, en, reset
  Multiplexer #(.width(16), .disabled(0), .enable("false")) multiplexer_2 (
    .in0(from_bus), .in1(multiplexer_1_out), .out(data_out), .sel(word));
  Multiplexer #(.width(16), .disabled(0), .enable("false")) multiplexer_3 (
    .in0(make_byte_2_out), .in1(n2s_compliment_1_out), .out(multiplexer_3_out), .sel(sign_extend));
  Multiplexer #(.width(16), .disabled(0), .enable("false")) multiplexer_4 (
    .in0(multiplexer_3_out), .in1(multiplexer_5_out), .out(to_bus), .sel(word));
  Multiplexer #(.width(16), .disabled(0), .enable("false")) multiplexer_5 (
    .in0(data_in), .in1({bit_extender_1_out, register_1_q}), .out(multiplexer_5_out), .sel(inc_address));

  assign phase = inc_address;

  // Other names for the same wires on the sheet: odd = odd_address

  // Notes on the sheet:
  //   data_in: pull=down
endmodule

module alu (
  input  [15:0] A,
  input  [15:0] B,
  input  Cin,
  input  [2:0] func,
  input  [2:0] op_type,
  input  [2:0] shift_count,
  output C,
  output V,
  output Z,
  output N,
  output [15:0] S
);

  wire adc, add, adder_c, adder_carry, adder_v, \and , and_3_out, and_4_out, and_5_out, and_6_out, bic,
       multiplexer_5_out, multiplexer_6_out, neg, \not , not_5_out, \or , or_2_out, or_3_out, rcl, rcr, rol,
       ror, sbc, scl, shifter_c, shl, shr, shra, sub, sxt, \xor ;
  wire [1:0] encoded_type;
  wire [15:0] adder_out, and_1_out, and_2_out, logic_out, make_byte_1_out, multiplexer_1_out,
       multiplexer_2_out, n2s_compliment_1_out, not_1_out, not_2_out, not_3_out, not_4_out, or_1_out,
       shifter_out, unary_out, xor_1_out;

  Decoder #(.select(3), .disabled(0)) decoder_1 (
    .out0(\and ), .out1(\or ), .out2(\xor ), .out3(bic), .out4(add), .out5(adc), .out6(sub), .out7(sbc),
    .sel(func), .en(op_type[0]));
  Decoder #(.select(3), .disabled(0)) decoder_2 (
    .out0(neg), .out1(\not ), .out2(sxt), .out3(scl), .sel(func), .en(op_type[1]));  // open: out4, out5, out6, out7
  Decoder #(.select(3), .disabled(0)) decoder_3 (
    .out0(shl), .out1(shr), .out2(shra), .out3(rol), .out4(ror), .out5(rcl), .out6(rcr), .sel(func),
    .en(op_type[2]));  // open: out7
  _2s_compliment u_2s_compliment_1 (.In(A), .Out(n2s_compliment_1_out));
  make_byte make_byte_1 (.In(A), .Out(make_byte_1_out));
  assign and_1_out = A & B;  // AND_Gate and_1, 16 bits wide
  assign or_1_out = A | B;  // OR_Gate or_1, 16 bits wide
  assign xor_1_out = A ^ B;  // XOR_Gate xor_1, 16 bits wide
  assign and_2_out = A & not_1_out;  // AND_Gate and_2, 16 bits wide
  assign not_1_out = ~B;  // NOT_Gate not_1, 16 bits wide
  Multiplexer #(.width(16), .enable("false")) multiplexer_1 (
    .in0(A), .in1(not_2_out), .out(multiplexer_1_out), .sel(neg));
  assign not_2_out = ~A;  // NOT_Gate not_2, 16 bits wide
  Multiplexer #(.width(16), .enable("false")) multiplexer_2 (
    .in0(B), .in1(not_3_out), .out(multiplexer_2_out), .sel(or_2_out));
  assign not_3_out = ~B;  // NOT_Gate not_3, 16 bits wide
  or or_2 (or_2_out, sub, sbc);
  assign not_4_out = ~A;  // NOT_Gate not_4, 16 bits wide
  barrel_shifter barrel_shifter_1 (
    .In(A), .cin(Cin), .shift_type(func), .distance(shift_count), .Out(shifter_out), .cout(shifter_c));
  adder16 adder16_1 (
    .A(multiplexer_1_out), .B(multiplexer_2_out), .S(adder_out), .Cin(adder_carry), .Cout(adder_c),
    .V(adder_v));
  Multiplexer #(.select(3), .width(16), .enable("false")) multiplexer_3 (
    .in0(adder_out), .in1(not_4_out), .in2(n2s_compliment_1_out), .in3(make_byte_1_out), .out(unary_out),
    .sel(func));  // open: in4, in5, in6, in7
  Multiplexer #(.select(2), .width(16), .enable("false")) multiplexer_4 (
    .in0(and_1_out), .in1(or_1_out), .in2(xor_1_out), .in3(and_2_out), .out(logic_out), .sel(func[1:0]));
  and and_3 (and_3_out, sbc, Cin);
  or or_3 (or_3_out, and_3_out, and_4_out);
  and and_4 (and_4_out, Cin, adc);
  or or_4 (adder_carry, or_3_out, neg, sub);
  not not_5 (not_5_out, func[2]);
  Multiplexer #(.enable("false")) multiplexer_5 (.in0(1'b0), .in1(adder_c), .out(multiplexer_5_out), .sel(neg));
  Multiplexer #(.enable("false")) multiplexer_6 (.in0(1'b0), .in1(adder_v), .out(multiplexer_6_out), .sel(neg));
  and and_5 (and_5_out, op_type[0], not_5_out);
  and and_6 (and_6_out, func[2], op_type[0]);
  Multiplexer #(.select(2), .width(16), .enable("false")) multiplexer_7 (
    .in0(logic_out), .in1(adder_out), .in2(unary_out), .in3(shifter_out), .out({N, S[14:0]}),
    .sel(encoded_type));
  Multiplexer #(.select(2), .enable("false")) multiplexer_8 (
    .in0(1'b0), .in1(adder_c), .in2(multiplexer_5_out), .in3(shifter_c), .out(C), .sel(encoded_type));
  Multiplexer #(.select(2), .enable("false")) multiplexer_9 (
    .in0(1'b0), .in1(adder_v), .in2(multiplexer_6_out), .in3(1'b0), .out(V), .sel(encoded_type));
  Priority_Encoder #(.select(2), .disabled(0)) priority_encoder_1 (
    .in0(and_5_out), .in1(and_6_out), .in2(op_type[1]), .in3(op_type[2]), .out(encoded_type));  // open: gs, en_out, en_in
  Pull_Resistor pull_resistor_1 (.node(encoded_type));
  // Probe on {N, S[14:0]}
  // NOT_Gate not_6 is placed but not wired
  zero16 zero16_1 (.in({N, S[14:0]}), .zero(Z));
  // NOT_Gate not_7 is placed but not wired

  assign S[15] = N;

  // Other names for the same wires on the sheet: _3op = op_type[0]; _2op = op_type[1]; shifts = op_type[2]

  // Notes on the sheet:
  //   B: pull=down
  //   func: pull=down
  //   Cin: pull=down
  //   A: pull=down
  //   shift_count: pull=down
  //   op_type: pull=down
endmodule

module barrel_shifter (
  input  [15:0] In,
  input  cin,
  input  [2:0] shift_type,
  input  [2:0] distance,
  output [15:0] Out,
  output cout
);

  wire [4:0] adder_1_out, bit_extender_1_out;
  wire [15:0] shifter_4_out, shifter_5_out;
  wire [16:0] shifter_1_out, shifter_2_out, shifter_3_out, shifter_6_out, shifter_7_out;

  assign bit_extender_1_out = {{2{1'b0}}, distance};  // Bit_Extender bit_extender_1
  Adder #(.width(5)) adder_1 (.a(bit_extender_1_out), .b(5'b00001), .out(adder_1_out));  // open: cin, cout
  Shifter #(.width(17)) shifter_1 (.in({{2{In[15]}}, In[14:0]}), .\dist (adder_1_out), .out(shifter_1_out));
  Shifter #(.width(17), .shift("lr")) shifter_2 (.in({In, In[0]}), .\dist (adder_1_out), .out(shifter_2_out));
  Shifter #(.width(17), .shift("ar")) shifter_3 (.in({In, In[0]}), .\dist (adder_1_out), .out(shifter_3_out));
  Shifter #(.width(16), .shift("rl")) shifter_4 (.in(In), .\dist (adder_1_out[3:0]), .out(shifter_4_out));
  Shifter #(.width(16), .shift("rr")) shifter_5 (.in(In), .\dist (adder_1_out[3:0]), .out(shifter_5_out));
  Shifter #(.width(17), .shift("rl")) shifter_6 (.in({cin, In}), .\dist (adder_1_out), .out(shifter_6_out));
  Shifter #(.width(17), .shift("rr")) shifter_7 (.in({In, cin}), .\dist (adder_1_out), .out(shifter_7_out));
  Multiplexer #(.select(3), .width(16), .enable("false")) multiplexer_1 (
    .in0(shifter_1_out[15:0]), .in1(shifter_2_out[16:1]), .in2(shifter_3_out[16:1]), .in3(shifter_4_out),
    .in4(shifter_5_out), .in5(shifter_6_out[15:0]), .in6(shifter_7_out[16:1]), .out(Out), .sel(shift_type));  // open: in7
  Multiplexer #(.select(3), .enable("false")) multiplexer_2 (
    .in0(shifter_1_out[16]), .in1(shifter_2_out[0]), .in2(shifter_3_out[0]), .in3(shifter_4_out[0]),
    .in4(shifter_5_out[15]), .in5(shifter_6_out[16]), .in6(shifter_7_out[0]), .out(cout), .sel(shift_type));  // open: in7

  // Other names for the same wires on the sheet: value[15:0] = In; type[2:0] = shift_type

  // Notes on the sheet:
  //   In: pull=down
  //   shift_type: pull=down
  //   distance: pull=down
  //   cin: pull=down
  //   shl
  //   shr
  //   shra
  //   rol
  //   ror
  //   rcl
  //   rcr
endmodule

module adder16 (
  input  Cin,
  input  [15:0] A,
  input  [15:0] B,
  output [15:0] S,
  output Cout,
  output V
);

  wire [15:0] and_1_out, and_2_out, and_3_out;
  wire [15:1] or_1_out;

  // Probe on A
  // Probe on B
  assign S = A ^ {or_1_out, Cin} ^ B;  // XOR_Gate xor_1, 16 bits wide
  assign and_1_out = B & A;  // AND_Gate and_1, 16 bits wide
  assign and_2_out = B & {or_1_out, Cin};  // AND_Gate and_2, 16 bits wide
  assign and_3_out = A & {or_1_out, Cin};  // AND_Gate and_3, 16 bits wide
  assign {Cout, or_1_out} = and_1_out | and_2_out | and_3_out;  // OR_Gate or_1, 16 bits wide
  // Probe on S
  xor xor_2 (V, or_1_out[15], Cout);

  // Notes on the sheet:
  //   A: pull=down
  //   Cin: pull=down
  //   B: pull=down
endmodule

module branch_logic (
  input  [3:0] cccc,
  input  [3:0] CVZN,
  output go
);

  wire and_1_out, and_2_out, and_3_out, and_4_out, and_5_out, and_6_out, and_7_out, decoder_1_out0,
       decoder_1_out1, decoder_1_out2, decoder_1_out3, decoder_2_out0, decoder_2_out1, decoder_2_out2,
       decoder_2_out3, not_1_out, not_2_out, or_1_out, xnor_1_out;

  not not_1 (not_1_out, cccc[3]);
  Decoder #(.select(2), .disabled(0)) decoder_1 (
    .out0(decoder_1_out0), .out1(decoder_1_out1), .out2(decoder_1_out2), .out3(decoder_1_out3),
    .sel(cccc[2:1]), .en(not_1_out));
  and and_1 (and_1_out, decoder_1_out0, CVZN[1]);
  and and_2 (and_2_out, decoder_1_out1, CVZN[3]);
  and and_3 (and_3_out, decoder_1_out2, CVZN[0]);
  and and_4 (and_4_out, decoder_1_out3, CVZN[2]);
  not not_2 (not_2_out, CVZN[1]);
  xnor xnor_1 (xnor_1_out, CVZN[0], CVZN[2]);
  Decoder #(.select(2), .disabled(0)) decoder_2 (
    .out0(decoder_2_out0), .out1(decoder_2_out1), .out2(decoder_2_out2), .out3(decoder_2_out3),
    .sel(cccc[2:1]), .en(cccc[3]));
  and and_5 (and_5_out, decoder_2_out0, not_2_out, CVZN[3]);
  and and_6 (and_6_out, xnor_1_out, decoder_2_out1);
  and and_7 (and_7_out, not_2_out, xnor_1_out, decoder_2_out2);
  or or_1 (or_1_out, and_1_out, and_2_out, and_3_out, and_4_out, and_5_out, and_6_out, and_7_out, decoder_2_out3);
  xor xor_1 (go, cccc[0], or_1_out);

  // Notes on the sheet:
  //   N
  //   Z
  //   V
  //   C
  //   EQ
  //   HS/CS
  //   MI
  //   VS
  //   N=V
  //   Z'
  //   HI
  //   GE
  //   GT
  //   <always>
endmodule

module zero16 (
  input  [15:0] in,
  output zero
);

  wire nor_1_out, nor_2_out;

  nor nor_1 (nor_1_out, in[0], in[1], in[2], in[3], in[4], in[5], in[6], in[7]);
  nor nor_2 (nor_2_out, in[8], in[9], in[10], in[11], in[12], in[13], in[14], in[15]);
  and and_1 (zero, nor_1_out, nor_2_out);
endmodule

module _2s_compliment (
  input  [15:0] In,
  output [15:0] Out
);

  wire [7:0] bit_extender_1_out;

  Bit_Extender #(.in_width(16), .out_width(8)) bit_extender_1 (.in(In), .out(bit_extender_1_out));
  assign Out = {{8{bit_extender_1_out[7]}}, bit_extender_1_out};  // Bit_Extender bit_extender_2
endmodule

module make_byte (
  input  [15:0] In,
  output [15:0] Out
);

  wire [7:0] bit_extender_1_out;

  Bit_Extender #(.in_width(16), .out_width(8)) bit_extender_1 (.in(In), .out(bit_extender_1_out));
  assign Out = {{8{1'b0}}, bit_extender_1_out};  // Bit_Extender bit_extender_2
endmodule

module bytes_swap (
  input  [15:0] In,
  output [15:0] Out
);


  assign Out = {In[7:0], In[15:8]};
endmodule

module sign_load (
  input  [15:0] in_1,
  output [15:0] out_2,
  output out_3
);

  wire [15:0] demultiplexer_1_out1, \output , output2;

  Demultiplexer #(.width(16), .enable("false")) demultiplexer_1 (
    .out0(\output ), .out1(demultiplexer_1_out1), .in(in_1), .sel(in_1[15]));
  Negator #(.width(16)) negator_1 (.in(demultiplexer_1_out1), .out(output2));
  Multiplexer #(.width(16), .enable("false")) multiplexer_1 (
    .in0(\output ), .in1(output2), .out(out_2), .sel(in_1[15]));

  assign out_3 = in_1[15];

  // Other names for the same wires on the sheet: isNeg = in_1[15]
endmodule
